// Digital circuit RAM (1).dig as structural Verilog
module RAM__1 (
  input  [7:0] M,
  input  [7:0] N,
  input  [12:0] progIN,
  input  reset,
  input  progLoad,
  input  start,
  input  result,
  input  clk,
  output [7:0] K,
  output valid,
  output done,
  output [7:0] \output ,
  output [12:0] out_13,
  output [7:0] out_14,
  output [7:0] out_15,
  output [4:0] out_16,
  output [7:0] accA,
  output [7:0] accB,
  output [7:0] regC,
  output [7:0] out_20,
  output [7:0] out_21,
  output equal,
  output greater,
  output lesser
);

  wire _0, _1, _2, _3, _4, _5, _6, _7, _8, _9, _10, _11, _12, _13, _14, _15, _16, _17, _18, _19, _20, _21,
       _22, _23, _24, _25, _26, _27, _28, _29, _30, _31, and_1_out, and_2_out, and_3_out, and_4_out,
       and_5_out, and_6_out, and_7_out, and_8_out, and_9_out, and_10_out, and_11_out, and_12_out,
       comparator_1_lt, comparator_3_eq, comparator_4_eq, comparator_4_gt, comparator_4_lt, d_ff_1_q,
       d_ff_2_q, d_ff_3_q, Done_t, multiplexer_11_out, multiplexer_12_out, multiplexer_13_out,
       multiplexer_14_out, multiplexer_15_out, multiplexer_16_out, multiplexer_17_out, not_1_out, not_2_out,
       or_1_out, or_2_out, or_3_out, or_4_out, or_5_out, or_9_out, or_10_out, or_11_out, or_13_out,
       or_14_out, or_15_out, reset0, reset1, reset1_0, result0, result1, result1_0, rom_1_d, startread0,
       startread1, startread1_0;
  wire [7:0] _2_com_2_comA_2_comB, _2_com_2_comA_plus_2_comB, _2_com_2_comB_2_comA, _2_comA, _2_comA_2_comB,
       _2_comA_plus_2_comB, _2_comB, _2_comB_2_comA, A_B, A_plus_B, add_1_s, add_2_s, add_3_s, add_5_s,
       add_6_s, add_7_s, Address1, AddressOperand1, AddressOperand2, and_13_out, barrelshifter_1_out,
       div_1_q, div_1_r, mul_1_mul, multiplexer_1_out, multiplexer_2_out, multiplexer_3_out,
       multiplexer_6_out, multiplexer_9_out, multiplexer_10_out, multiplexer_18_out, multiplexer_23_out,
       multiplexer_24_out, multiplexer_25_out, multiplexer_26_out, multiplexer_27_out, multiplexer_28_out,
       multiplexer_30_out, multiplexer_31_out, multiplexer_32_out, multiplexer_35_out, multiplexer_36_out,
       multiplexer_37_out, multiplexer_38_out, multiplexer_39_out, multiplexer_40_out, multiplexer_41_out,
       multiplexer_42_out, multiplexer_43_out, multiplexer_44_out, multiplexer_45_out, multiplexer_46_out,
       Operand, or_12_out, rom_2_d, Value2, xor_1_out, xor_2_out, xor_3_out, xor_4_out, xor_5_out, xor_6_out,
       xor_7_out;
  wire [12:0] multiplexer_19_out, Value1;

  Add #(.Bits(8)) add_1 (.a(K), .b(8'h1), .c_i(1'b0), .s(add_1_s));  // open: c_o
  assign xor_1_out = accA ^ {8{1'b1}};  // XOr xor_1, 8 bits wide
  assign xor_2_out = accB ^ {8{1'b1}};  // XOr xor_2, 8 bits wide
  Add #(.Bits(8)) add_2 (.a(out_21), .b(8'h1), .c_i(1'b0), .s(add_2_s));  // open: c_o
  Add #(.Bits(8)) add_3 (.a(out_14), .b(8'h1), .c_i(1'b0), .s(add_3_s));  // open: c_o
  Multiplexer #(.Bits(8)) multiplexer_1 (.sel(reset), .in_0(add_1_s), .in_1({8{1'b0}}), .out(multiplexer_1_out));
  or or_1 (or_1_out, greater, equal);
  Sub #(.Bits(8)) sub_1 (.a(_2_comB), .b(_2_comA), .c_i(1'b0), .s(_2_comB_2_comA));  // open: c_o
  Sub #(.Bits(8)) sub_2 (.a(_2_comA), .b(_2_comB), .c_i(1'b0), .s(_2_comA_2_comB));  // open: c_o
  Add #(.Bits(8)) add_4 (.a(_2_comA), .b(_2_comB), .c_i(1'b0), .s(_2_comA_plus_2_comB));  // open: c_o
  Multiplexer #(.Bits(8)) multiplexer_2 (.sel(result1), .in_0({8{1'b0}}), .in_1(add_2_s), .out(multiplexer_2_out));
  Multiplexer #(.Bits(8)) multiplexer_3 (.sel(reset1), .in_0({8{1'b0}}), .in_1(add_3_s), .out(multiplexer_3_out));
  or or_2 (or_2_out, progLoad, reset);
  and and_1 (and_1_out, _13, equal);
  and and_2 (and_2_out, _14, greater);
  and and_3 (and_3_out, _15, lesser);
  and and_4 (and_4_out, _16, or_1_out);
  Add #(.Bits(8)) add_5 (.a(xor_1_out), .b(8'h1), .c_i(1'b0), .s(add_5_s));  // open: c_o
  Add #(.Bits(8)) add_6 (.a(xor_2_out), .b(8'h1), .c_i(1'b0), .s(add_6_s));  // open: c_o
  Register #(.Bits(8)) register_1 (.D(multiplexer_2_out), .C(clk), .en(result1_0), .Q(out_21));
  Register #(.Bits(8)) register_2 (.D(multiplexer_3_out), .C(clk), .en(reset1_0), .Q(out_14));
  Comparator #(.Bits(8)) comparator_1 (.a(K), .b(8'hf), .lt(comparator_1_lt));  // open: gt, eq
  Register #(.Bits(8)) register_3 (.D(multiplexer_1_out), .C(clk), .en(or_2_out), .Q(K));
  Multiplexer #(.Bits(8)) multiplexer_4 (.sel(accA[7]), .in_0(accA), .in_1(add_5_s), .out(_2_comA));
  Multiplexer #(.Bits(8)) multiplexer_5 (.sel(accB[7]), .in_0(accB), .in_1(add_6_s), .out(_2_comB));
  Multiplexer #(.Bits(8)) multiplexer_6 (.sel(comparator_1_lt), .in_0(K), .in_1(8'hf), .out(multiplexer_6_out));
  or or_3 (or_3_out, _12, and_1_out, and_2_out, and_3_out, and_4_out);
  Comparator #(.Bits(8)) comparator_2 (.a(out_21), .b(8'hf), .eq(Done_t));  // open: gt, lt
  Comparator #(.Bits(8)) comparator_3 (.a(out_14), .b(multiplexer_6_out), .eq(comparator_3_eq));  // open: gt, lt
  not not_1 (not_1_out, Done_t);
  not not_2 (not_2_out, comparator_3_eq);
  Multiplexer #(.Selector_Bits(2), .Bits(8)) multiplexer_7 (
    .sel({accB[7], accA[7]}), .in_0(_2_com_2_comA_2_comB), .in_1(_2_com_2_comA_plus_2_comB),
    .in_2(_2_comA_plus_2_comB), .in_3(_2_com_2_comB_2_comA), .out(A_B));
  Multiplexer #(.Selector_Bits(2), .Bits(8)) multiplexer_8 (
    .sel({accB[7], accA[7]}), .in_0(_2_comA_plus_2_comB), .in_1(_2_com_2_comB_2_comA),
    .in_2(_2_com_2_comA_2_comB), .in_3(_2_com_2_comA_plus_2_comB), .out(A_plus_B));
  Add #(.Bits(8)) add_7 (.a(out_15), .b(8'h1), .c_i(1'b0), .s(add_7_s));  // open: c_o
  Multiplexer #(.Bits(8)) multiplexer_9 (
    .sel(or_3_out), .in_0(multiplexer_10_out), .in_1(Operand), .out(multiplexer_9_out));
  and and_5 (and_5_out, not_1_out, d_ff_1_q);
  and and_6 (and_6_out, not_1_out, result, ~d_ff_1_q);  // And
  and and_7 (and_7_out, not_2_out, d_ff_2_q);
  and and_8 (and_8_out, not_2_out, reset, ~d_ff_2_q);  // And
  Multiplexer #(.Bits(8)) multiplexer_10 (.sel(startread1), .in_0({8{1'b0}}), .in_1(add_7_s), .out(multiplexer_10_out));
  Register #(.Bits(8)) register_4 (.D(multiplexer_9_out), .C(clk), .en(startread1_0), .Q(out_15));
  assign xor_3_out = _2_comA_plus_2_comB ^ {8{1'b1}};  // XOr xor_3, 8 bits wide
  assign xor_4_out = _2_comB_2_comA ^ {8{1'b1}};  // XOr xor_4, 8 bits wide
  assign xor_5_out = _2_comA_2_comB ^ {8{1'b1}};  // XOr xor_5, 8 bits wide
  or or_4 (or_4_out, and_5_out, and_6_out);
  D_FF d_ff_1 (.D(or_4_out), .C(clk), .Q(d_ff_1_q));  // open: nQ
  or or_5 (or_5_out, and_7_out, and_8_out);
  Decoder #(.Selector_Bits(5)) decoder_1 (
    .sel(out_16), .out_0(_0), .out_1(_1), .out_2(_2), .out_3(_3), .out_4(_4), .out_5(_5), .out_6(_6),
    .out_7(_7), .out_8(_8), .out_9(_9), .out_10(_10), .out_11(_11), .out_12(_12), .out_13(_13), .out_14(_14),
    .out_15(_15), .out_16(_16), .out_17(_17), .out_18(_18), .out_19(_19), .out_20(_20), .out_21(_21),
    .out_22(_22), .out_23(_23), .out_24(_24), .out_25(_25), .out_26(_26), .out_27(_27), .out_28(_28),
    .out_29(_29), .out_30(_30), .out_31(_31));
  Add #(.Bits(8)) add_8 (.a(xor_3_out), .b(8'h1), .c_i(1'b0), .s(_2_com_2_comA_plus_2_comB));  // open: c_o
  Add #(.Bits(8)) add_9 (.a(xor_4_out), .b(8'h1), .c_i(1'b0), .s(_2_com_2_comB_2_comA));  // open: c_o
  Add #(.Bits(8)) add_10 (.a(xor_5_out), .b(8'h1), .c_i(1'b0), .s(_2_com_2_comA_2_comB));  // open: c_o
  D_FF d_ff_2 (.D(or_5_out), .C(clk), .Q(d_ff_2_q));  // open: nQ
  Decoder decoder_2 (.sel(d_ff_1_q), .out_0(result0), .out_1(result1));
  Decoder decoder_3 (.sel(d_ff_2_q), .out_0(reset0), .out_1(reset1));
  Decoder decoder_4 (.sel(d_ff_3_q), .out_0(startread0), .out_1(startread1));
  and and_9 (and_9_out, ~d_ff_3_q, start);  // And
  and and_10 (and_10_out, d_ff_3_q, ~_31);  // And
  Comparator #(.Bits(8)) comparator_4 (
    .a(_2_comA), .b(_2_comB), .gt(comparator_4_gt), .eq(comparator_4_eq), .lt(comparator_4_lt));
  or or_6 (result1_0, result0, result1);
  or or_7 (reset1_0, reset0, reset1);
  or or_8 (startread1_0, startread0, startread1);
  D_FF d_ff_3 (.D(or_9_out), .C(clk), .Q(d_ff_3_q));  // open: nQ
  or or_9 (or_9_out, and_9_out, and_10_out);
  Multiplexer #(.Selector_Bits(2)) multiplexer_11 (
    .sel({accB[7], accA[7]}), .in_0(comparator_4_eq), .in_1(1'b0), .in_2(1'b0), .in_3(comparator_4_eq),
    .out(multiplexer_11_out));
  Multiplexer #(.Selector_Bits(2)) multiplexer_12 (
    .sel({accB[7], accA[7]}), .in_0(comparator_4_lt), .in_1(1'b1), .in_2(1'b0), .in_3(comparator_4_gt),
    .out(multiplexer_12_out));
  Multiplexer #(.Selector_Bits(2)) multiplexer_13 (
    .sel({accB[7], accA[7]}), .in_0(comparator_4_gt), .in_1(1'b0), .in_2(1'b1), .in_3(comparator_4_lt),
    .out(multiplexer_13_out));
  Multiplexer multiplexer_14 (.sel(_23), .in_0(1'b0), .in_1(multiplexer_11_out), .out(multiplexer_14_out));
  ROM #(.AddrBits(8)) rom_1 (.A(accA), .sel(1'b1), .D(rom_1_d));
  Multiplexer multiplexer_15 (.sel(_23), .in_0(1'b0), .in_1(multiplexer_12_out), .out(multiplexer_15_out));
  Multiplexer multiplexer_16 (.sel(_23), .in_0(1'b0), .in_1(multiplexer_13_out), .out(multiplexer_16_out));
  Multiplexer multiplexer_17 (.sel(_29), .in_0(multiplexer_14_out), .in_1(rom_1_d), .out(multiplexer_17_out));
  or or_10 (or_10_out, _29, _23);
  Multiplexer #(.Bits(8)) multiplexer_18 (.sel(progLoad), .in_0(out_14), .in_1(K), .out(multiplexer_18_out));
  Multiplexer #(.Bits(13)) multiplexer_19 (.sel(progLoad), .in_0({13{1'b0}}), .in_1(progIN), .out(multiplexer_19_out));
  Multiplexer #(.Bits(8)) multiplexer_20 (.sel(_10), .in_0(Address1), .in_1(Operand), .out(AddressOperand1));
  Register register_5 (.D(multiplexer_15_out), .C(clk), .en(_23), .Q(lesser));
  Register register_6 (.D(multiplexer_16_out), .C(clk), .en(_23), .Q(greater));
  Register register_7 (.D(multiplexer_17_out), .C(clk), .en(or_10_out), .Q(equal));
  Multiplexer #(.Bits(8)) multiplexer_21 (.sel(startread1), .in_0(multiplexer_18_out), .in_1(out_15), .out(Address1));
  Multiplexer #(.Bits(13)) multiplexer_22 (
    .sel(startread1), .in_0(multiplexer_19_out), .in_1({out_16, Operand}), .out(Value1));
  or or_11 (or_11_out, progLoad, reset1);
  Div #(.Bits(8)) div_1 (.a(accA), .b(accB), .q(div_1_q), .r(div_1_r));
  Multiplexer #(.Bits(8)) multiplexer_23 (.sel(_1), .in_0({8{1'b0}}), .in_1(Operand), .out(multiplexer_23_out));
  Multiplexer #(.Bits(8)) multiplexer_24 (
    .sel(_20), .in_0(multiplexer_42_out), .in_1(div_1_q), .out(multiplexer_24_out));
  ROM #(.AddrBits(6), .Bits(8)) rom_2 (.A({accA[2:0], accB[2:0]}), .sel(1'b1), .D(rom_2_d));
  RAMDualAccess #(.AddrBits(8), .Bits(13)) pRAM (
    .str(or_11_out), .C(clk), .ld(startread1), .A1(Address1), .Din1(Value1), .A2(AddressOperand1),
    .D1({out_16, Operand}), .D2(out_13));
  RAMDualAccess #(.AddrBits(8), .Bits(8)) rRAM (
    .str(_11), .C(clk), .ld(1'b0), .A1(AddressOperand2), .Din1(Value2), .A2(AddressOperand2), .D2(out_20));  // open: D1
  and and_11 (and_11_out, Done_t, ~reset, ~start);  // And
  and and_12 (and_12_out, ~reset, ~start, _31);  // And
  Multiplexer #(.Bits(8)) multiplexer_25 (.sel(_3), .in_0(multiplexer_23_out), .in_1(accB), .out(multiplexer_25_out));
  Multiplexer #(.Bits(8)) multiplexer_26 (
    .sel(_21), .in_0(multiplexer_24_out), .in_1(div_1_r), .out(multiplexer_26_out));
  Register register_8 (.D(and_11_out), .C(clk), .en(and_11_out), .Q(done));
  Register register_9 (.D(and_12_out), .C(clk), .en(and_12_out), .Q(valid));
  Multiplexer #(.Bits(8)) multiplexer_27 (.sel(_6), .in_0(multiplexer_25_out), .in_1(regC), .out(multiplexer_27_out));
  Multiplexer #(.Bits(8)) multiplexer_28 (
    .sel(_22), .in_0(multiplexer_26_out), .in_1(rom_2_d), .out(multiplexer_28_out));
  assign xor_6_out = accA ^ {8{1'b1}};  // XOr xor_6, 8 bits wide
  Multiplexer #(.Bits(8)) multiplexer_29 (.sel(result1), .in_0({8{1'b0}}), .in_1(out_20), .out(\output ));
  Multiplexer #(.Bits(8)) multiplexer_30 (.sel(_9), .in_0(multiplexer_27_out), .in_1(out_20), .out(multiplexer_30_out));
  Multiplexer #(.Bits(8)) multiplexer_31 (
    .sel(_24), .in_0(multiplexer_28_out), .in_1(xor_6_out), .out(multiplexer_31_out));
  assign or_12_out = accA | accB;  // Or or_12, 8 bits wide
  Multiplexer #(.Bits(8)) multiplexer_32 (
    .sel(_10), .in_0(multiplexer_30_out), .in_1(out_13[7:0]), .out(multiplexer_32_out));
  Multiplexer #(.Bits(8)) multiplexer_33 (.sel(result1), .in_0(Operand), .in_1(out_21), .out(AddressOperand2));
  Multiplexer #(.Bits(8)) multiplexer_34 (.sel(_11), .in_0({8{1'b0}}), .in_1(accA), .out(Value2));
  Seven_Seg_Hex seven_seg_hex_1 (.d(\output [7:4]), .dp(1'b0));
  Multiplexer #(.Bits(8)) multiplexer_35 (
    .sel(_25), .in_0(multiplexer_31_out), .in_1(or_12_out), .out(multiplexer_35_out));
  assign and_13_out = accA & accB;  // And and_13, 8 bits wide
  Multiplexer #(.Bits(8)) multiplexer_36 (
    .sel(_17), .in_0(multiplexer_32_out), .in_1(A_plus_B), .out(multiplexer_36_out));
  Multiplexer #(.Bits(8)) multiplexer_37 (
    .sel(_26), .in_0(multiplexer_35_out), .in_1(and_13_out), .out(multiplexer_37_out));
  assign xor_7_out = accA ^ accB;  // XOr xor_7, 8 bits wide
  Seven_Seg_Hex seven_seg_hex_2 (.d(\output [3:0]), .dp(1'b0));
  Multiplexer #(.Bits(8)) multiplexer_38 (.sel(_18), .in_0(multiplexer_36_out), .in_1(A_B), .out(multiplexer_38_out));
  Mul #(.Bits(4), .Signed("true")) mul_1 (.a(accA[3:0]), .b(accB[3:0]), .mul(mul_1_mul));
  Multiplexer #(.Bits(8)) multiplexer_39 (
    .sel(_27), .in_0(multiplexer_37_out), .in_1(xor_7_out), .out(multiplexer_39_out));
  Multiplexer #(.Bits(8)) multiplexer_40 (.sel(_5), .in_0({8{1'b0}}), .in_1(accA), .out(multiplexer_40_out));
  Multiplexer #(.Bits(8)) multiplexer_41 (.sel(_2), .in_0({8{1'b0}}), .in_1(Operand), .out(multiplexer_41_out));
  Multiplexer #(.Bits(8)) multiplexer_42 (
    .sel(_19), .in_0(multiplexer_38_out), .in_1(mul_1_mul), .out(multiplexer_42_out));
  Multiplexer #(.Bits(8)) multiplexer_43 (
    .sel(_28), .in_0(multiplexer_39_out), .in_1(barrelshifter_1_out), .out(multiplexer_43_out));
  BarrelShifter #(.Bits(8), .barrelShifterMode("rotate")) barrelshifter_1 (
    .in(accA), .shift({1'b0, accB[2:0]}), .out(barrelshifter_1_out));
  Multiplexer #(.Bits(8)) multiplexer_44 (.sel(_7), .in_0(multiplexer_40_out), .in_1(M), .out(multiplexer_44_out));
  Multiplexer #(.Bits(8)) multiplexer_45 (.sel(_8), .in_0(multiplexer_44_out), .in_1(N), .out(multiplexer_45_out));
  Multiplexer #(.Bits(8)) multiplexer_46 (.sel(_4), .in_0(multiplexer_41_out), .in_1(accA), .out(multiplexer_46_out));
  or or_13 (or_13_out, _2, _4);
  or or_14 (or_14_out, _1, _3, _6, _9, _10, _17, _18, _19, _20, _21, _22, _24, _25, _26, _27, _28);
  or or_15 (or_15_out, _5, _7, _8);
  Register #(.Bits(8)) register_10 (.D(multiplexer_46_out), .C(clk), .en(or_13_out), .Q(accB));
  Register #(.Bits(8)) register_11 (.D(multiplexer_43_out), .C(clk), .en(or_14_out), .Q(accA));
  Register #(.Bits(8)) register_12 (.D(multiplexer_45_out), .C(clk), .en(or_15_out), .Q(regC));

  // Other names for the same wires on the sheet: ReadAddress[7:0] = out_15; ReadAddressOperand1[12:0] = out_13;
  //   ReadAddressOperand2[7:0] = out_20; ReadValue1[12:0] = {out_16, Operand}; ResetAddress[7:0] = out_14;
  //   ResultAddress[7:0] = out_21; StartRead = start; StartWrite = progLoad; WriteAddress[7:0] = K;
  //   WriteValue[12:0] = progIN

  // Notes on the sheet:
  //   progIN: default 1
  //   Result
  //   Reset
  //   Write
  //   Jump
  //   CO-OP999
  //   6733185821 Penpitcha Piyawaranont
  //   6733255021 Sirikarn Fugsrimuang
  //   6733284221 Atipat Buranavatanachoke
  //   6733293921 Aitsayaphan Limmuangnil
  //   2's complement
  //   Read
  //   Greater Lesser Equal
  //   Write Adress and Value RAM1
  //   contents of rom_1 (hex, n*v repeats v):
  //   0,0,1,1,0,1,0,1,0,a,a,1,a,1,a,a,0,1,4,1,10,20,40,1,0,4*a,1,0,1
  //   ,0,4,10,40,0,1,0,0,0,1,a,1,0,0,0,1,0,6,24,d8,0,1,0,0,0,a,a,1,0
  //   ,1,5*0,1,0,0,0,1,0,1,5*0,1,0,0,0,1,5*0,1,7*0,1,0,0,0,1,0,1,0,0,0
  //   ,b,0,1,0,0,0,1,13*0,1,0,0,0,1,5*0,1,0,1,9*0,1,0,1,5*0,1,5*0,1
  //   ,0,0,0,1,5*0,1,5*0,1,0,1,9*0,1,0,1,0,0,0,1,0,1,11*0,1,11*0,1,0,0,0
  //   ,1,0,1,0,0,0,1,5*0,1,0,1,9*0,1
  //   0-reset 1-write
  //   A
  //   1-read
  //   contents of rom_2 (hex, n*v repeats v):
  //   9*0,7*1,0,2,4,8,10,20,40,80,0,3,9,1b,51,f3,0,0,0,4,10,40,5*0,5
  //   ,19,7d,5*0,6,24,d8,5*0,7,31
  //   Write Adress and Value RAM2
  //   0-writeOperand
  //   1-result
  //   AllTask
  //   C
  //   B
endmodule

/* Test case 01_P01T01:
M N progIN reset progLoad start result clk valid done output
0 0 0 0 0 0 0 0 0 0 0
0 0 0 0 0 0 0 1 0 0 0
0 0 0 1 0 0 0 0 0 0 0
0 0 0 1 0 0 0 1 0 0 0
0 0 0 0 0 0 0 0 0 0 0
0 0 0 0 0 0 0 1 0 0 0
0 0 0 0 0 0 0 0 0 0 0
0 0 0 0 0 0 0 1 0 0 0
0 0 0 0 0 0 0 0 0 0 0
0 0 0 0 0 0 0 1 0 0 0
0 0 0 0 0 0 0 0 0 0 0
0 0 0 0 0 0 0 1 0 0 0
0 0 0 0 0 0 0 0 0 0 0
0 0 0 0 0 0 0 1 0 0 0
0 0 0 0 0 0 0 0 0 0 0
0 0 0 0 0 0 0 1 0 0 0
0 0 0 0 0 0 0 0 0 0 0
0 0 0 0 0 0 0 1 0 0 0
0 0 0 0 0 0 0 0 0 0 0
0 0 0 0 0 0 0 1 0 0 0
0 0 0 0 0 0 0 0 0 0 0
0 0 0 0 0 0 0 1 0 0 0
0 0 0 0 0 0 0 0 0 0 0
0 0 0 0 0 0 0 1 0 0 0
0 0 0 0 0 0 0 0 0 0 0
0 0 0 0 0 0 0 1 0 0 0
0 0 0 0 0 0 0 0 0 0 0
0 0 0 0 0 0 0 1 0 0 0
0 0 0 0 0 0 0 0 0 0 0
0 0 0 0 0 0 0 1 0 0 0
0 0 0 0 0 0 0 0 0 0 0
0 0 0 0 0 0 0 1 0 0 0
0 0 0 0 0 0 0 0 0 0 0
0 0 0 0 0 0 0 1 0 0 0
0 0 0 0 0 0 0 0 0 0 0
0 0 0 0 0 0 0 1 0 0 0
0 0 0 0 0 0 0 0 0 0 0
0 0 0 0 0 0 0 1 0 0 0
0 0 0 0 0 0 0 0 0 0 0
0 0 0 0 0 0 0 1 0 0 0
0 0 0 0 0 0 0 0 0 0 0
0 0 0 0 0 0 0 1 0 0 0
0 0 271 0 1 0 0 0 0 0 0
0 0 0 0 1 0 0 1 0 0 0
0 0 565 0 1 0 0 0 0 0 0
0 0 0 0 1 0 0 1 0 0 0
0 0 4352 0 1 0 0 0 0 0 0
0 0 0 0 1 0 0 1 0 0 0
0 0 2819 0 1 0 0 0 0 0 0
0 0 0 0 1 0 0 1 0 0 0
0 0 7936 0 1 0 0 0 0 0 0
0 0 0 0 1 0 0 1 0 0 0
0 0 0 0 0 1 0 0 0 0 0
0 0 0 0 0 1 0 1 0 0 0
0 0 0 0 0 0 0 0 x 0 0
0 0 0 0 0 0 0 1 x 0 0
0 0 0 0 0 0 0 0 x 0 0
0 0 0 0 0 0 0 1 x 0 0
0 0 0 0 0 0 0 0 x 0 0
0 0 0 0 0 0 0 1 x 0 0
0 0 0 0 0 0 0 0 x 0 0
0 0 0 0 0 0 0 1 x 0 0
0 0 0 0 0 0 0 0 x 0 0
0 0 0 0 0 0 0 1 x 0 0
0 0 0 0 0 0 0 0 x 0 0
0 0 0 0 0 0 0 1 x 0 0
0 0 0 0 0 0 0 0 x 0 0
0 0 0 0 0 0 0 1 x 0 0
0 0 0 0 0 0 0 0 x 0 0
0 0 0 0 0 0 0 1 x 0 0
0 0 0 0 0 0 0 0 x 0 0
0 0 0 0 0 0 0 1 x 0 0
0 0 0 0 0 0 0 0 x 0 0
0 0 0 0 0 0 0 1 x 0 0
0 0 0 0 0 0 0 0 x 0 0
0 0 0 0 0 0 0 1 x 0 0
0 0 0 0 0 0 0 0 x 0 0
0 0 0 0 0 0 0 1 x 0 0
0 0 0 0 0 0 0 0 x 0 0
0 0 0 0 0 0 0 1 x 0 0
0 0 0 0 0 0 0 0 x 0 0
0 0 0 0 0 0 0 1 x 0 0
0 0 0 0 0 0 0 0 x 0 0
0 0 0 0 0 0 0 1 x 0 0
0 0 0 0 0 0 0 0 x 0 0
0 0 0 0 0 0 0 1 x 0 0
0 0 0 0 0 0 0 0 x 0 0
0 0 0 0 0 0 0 1 x 0 0
0 0 0 0 0 0 0 0 x 0 0
0 0 0 0 0 0 0 1 x 0 0
0 0 0 0 0 0 0 0 x 0 0
0 0 0 0 0 0 0 1 x 0 0
0 0 0 0 0 0 0 0 x 0 0
0 0 0 0 0 0 0 1 x 0 0
0 0 0 0 0 0 0 0 x 0 0
0 0 0 0 0 0 0 1 x 0 0
0 0 0 0 0 0 0 0 x 0 0
0 0 0 0 0 0 0 1 x 0 0
0 0 0 0 0 0 0 0 x 0 0
0 0 0 0 0 0 0 1 x 0 0
0 0 0 0 0 0 0 0 x 0 0
0 0 0 0 0 0 0 1 x 0 0
0 0 0 0 0 0 0 0 x 0 0
0 0 0 0 0 0 0 1 x 0 0
0 0 0 0 0 0 0 0 x 0 0
0 0 0 0 0 0 0 1 1 0 0
0 0 0 0 0 0 1 0 1 0 0
0 0 0 0 0 0 1 1 1 0 0
0 0 0 0 0 0 0 0 1 0 0
0 0 0 0 0 0 0 1 1 0 0
0 0 0 0 0 0 0 0 1 0 0
0 0 0 0 0 0 0 1 1 0 0
0 0 0 0 0 0 0 0 1 0 0
0 0 0 0 0 0 0 1 1 0 68
0 0 0 0 0 0 0 0 1 0 68
0 0 0 0 0 0 0 1 1 0 0
0 0 0 0 0 0 0 0 1 0 0
0 0 0 0 0 0 0 1 1 0 0
0 0 0 0 0 0 0 0 1 0 0
0 0 0 0 0 0 0 1 1 0 0
0 0 0 0 0 0 0 0 1 0 0
0 0 0 0 0 0 0 1 1 0 0
0 0 0 0 0 0 0 0 1 0 0
0 0 0 0 0 0 0 1 1 0 0
0 0 0 0 0 0 0 0 1 0 0
0 0 0 0 0 0 0 1 1 0 0
0 0 0 0 0 0 0 0 1 0 0
0 0 0 0 0 0 0 1 1 0 0
0 0 0 0 0 0 0 0 1 0 0
0 0 0 0 0 0 0 1 1 0 0
0 0 0 0 0 0 0 0 1 0 0
0 0 0 0 0 0 0 1 1 0 0
0 0 0 0 0 0 0 0 1 0 0
0 0 0 0 0 0 0 1 1 0 0
0 0 0 0 0 0 0 0 1 0 0
0 0 0 0 0 0 0 1 1 0 0
0 0 0 0 0 0 0 0 1 0 0
0 0 0 0 0 0 0 1 1 0 0
0 0 0 0 0 0 0 0 1 0 0
0 0 0 0 0 0 0 1 1 1 0
0 0 0 0 0 0 0 0 1 1 0
0 0 0 0 0 0 0 1 1 1 0
0 0 0 0 0 0 0 0 1 1 0
*/
