// Digital circuit minicpu.dig as structural Verilog
module minicpu (
  input  [7:0] M,
  input  [7:0] N,
  input  [12:0] progIN,
  input  reset,
  input  progLoad,
  input  start,
  input  result,
  input  clk,
  output [7:0] K,
  output valid,
  output done,
  output [7:0] \output ,
  output [12:0] out_13,
  output [7:0] out_14,
  output [7:0] out_15,
  output [4:0] out_16,
  output [7:0] accA,
  output [7:0] accB,
  output [7:0] regC,
  output [7:0] out_20,
  output [7:0] out_21,
  output equal,
  output greater,
  output lesser,
  output out_25,
  output [7:0] gcd,
  output [15:0] lcm,
  output _30
);

  wire _0, _1, _2, _3, _4, _5, _6, _7, _8, _9, _10, _11, _12, _13, _14, _15, _16, _17, _18, _19, _20, _21,
       _22, _23, _24, _25, _26, _27, _28, _29, _30_t, _31, and_1_out, and_2_out, and_3_out, and_4_out,
       and_5_out, and_6_out, and_7_out, and_8_out, and_9_out, and_10_out, and_11_out, and_13_out, and_14_out,
       and_15_out, and_16_out, and_17_out, comparator_1_lt, comparator_3_eq, comparator_4_eq,
       comparator_4_gt, comparator_4_lt, comparator_5_eq, comparator_5_gt, counter0, counter1, counter2,
       counter3, d_ff_1_q, d_ff_2_q, d_ff_3_q, decoder_5_out_0, decoder_5_out_1, decoder_5_out_2,
       decoder_5_out_3, Done_t, multiplexer_11_out, multiplexer_12_out, multiplexer_13_out,
       multiplexer_14_out, multiplexer_18_out, multiplexer_19_out, multiplexer_20_out, multiplexer_56_out,
       multiplexer_58_out, not_1_out, not_2_out, or_1_out, or_2_out, or_3_out, or_4_out, or_5_out, or_9_out,
       or_10_out, or_11_out, or_12_out, or_13_out, or_14_out, or_16_out, or_17_out, or_18_out, or_19_out,
       or_20_out, or_21_out, register_18_q, reset0, reset1, reset1_0, result0, result1, result1_0, rom_1_d,
       startread0, startread1, startread1_0;
  wire [1:0] counter_1_out, d_ff_4_q;
  wire [7:0] _2_com_2_comA_2_comB, _2_com_2_comA_plus_2_comB, _2_com_2_comB_2_comA, _2_comA, _2_comA_2_comB,
       _2_comA_plus_2_comB, _2_comB, _2_comB_2_comA, A_B, A_plus_B, add_1_s, add_2_s, add_3_s, add_5_s,
       add_6_s, add_7_s, Address1, Address2, AddressOperand1, AddressOperand2, and_12_out,
       barrelshifter_1_out, div_1_q, div_1_r, mul_1_mul, multiplexer_1_out, multiplexer_2_out,
       multiplexer_3_out, multiplexer_6_out, multiplexer_9_out, multiplexer_10_out, multiplexer_15_out,
       multiplexer_23_out, multiplexer_24_out, multiplexer_25_out, multiplexer_26_out, multiplexer_27_out,
       multiplexer_28_out, multiplexer_29_out, multiplexer_30_out, multiplexer_33_out, multiplexer_34_out,
       multiplexer_35_out, multiplexer_36_out, multiplexer_37_out, multiplexer_39_out, multiplexer_40_out,
       multiplexer_41_out, multiplexer_42_out, multiplexer_43_out, multiplexer_45_out, multiplexer_46_out,
       multiplexer_47_out, multiplexer_48_out, multiplexer_49_out, multiplexer_50_out, multiplexer_51_out,
       multiplexer_52_out, multiplexer_53_out, multiplexer_54_out, multiplexer_55_out, multiplexer_57_out,
       Operand, or_15_out, ReadValue2, register_8_q, register_9_q, register_16_q, register_17_q, rom_2_d,
       sub_3_s, sub_4_s, Value2, xor_1_out, xor_2_out, xor_3_out, xor_4_out, xor_5_out, xor_6_out, xor_7_out;
  wire [12:0] multiplexer_16_out, pRAM_d1, Value1;
  wire [15:0] div_2_q, mul_2_mul;

  Add #(.Bits(8)) add_1 (.a(K), .b(8'h1), .c_i(1'b0), .s(add_1_s));  // open: c_o
  assign xor_1_out = accA ^ {8{1'b1}};  // XOr xor_1, 8 bits wide
  assign xor_2_out = accB ^ {8{1'b1}};  // XOr xor_2, 8 bits wide
  Add #(.Bits(8)) add_2 (.a(out_21), .b(8'h1), .c_i(1'b0), .s(add_2_s));  // open: c_o
  Add #(.Bits(8)) add_3 (.a(out_14), .b(8'h1), .c_i(1'b0), .s(add_3_s));  // open: c_o
  Multiplexer #(.Bits(8)) multiplexer_1 (.sel(reset), .in_0(add_1_s), .in_1({8{1'b0}}), .out(multiplexer_1_out));
  or or_1 (or_1_out, greater, equal);
  Sub #(.Bits(8)) sub_1 (.a(_2_comB), .b(_2_comA), .c_i(1'b0), .s(_2_comB_2_comA));  // open: c_o
  Sub #(.Bits(8)) sub_2 (.a(_2_comA), .b(_2_comB), .c_i(1'b0), .s(_2_comA_2_comB));  // open: c_o
  Add #(.Bits(8)) add_4 (.a(_2_comA), .b(_2_comB), .c_i(1'b0), .s(_2_comA_plus_2_comB));  // open: c_o
  Multiplexer #(.Bits(8)) multiplexer_2 (.sel(result1), .in_0({8{1'b0}}), .in_1(add_2_s), .out(multiplexer_2_out));
  Multiplexer #(.Bits(8)) multiplexer_3 (.sel(reset1), .in_0({8{1'b0}}), .in_1(add_3_s), .out(multiplexer_3_out));
  or or_2 (or_2_out, progLoad, reset);
  and and_1 (and_1_out, _13, equal);
  and and_2 (and_2_out, _14, greater);
  and and_3 (and_3_out, _15, lesser);
  and and_4 (and_4_out, _16, or_1_out);
  Add #(.Bits(8)) add_5 (.a(xor_1_out), .b(8'h1), .c_i(1'b0), .s(add_5_s));  // open: c_o
  Add #(.Bits(8)) add_6 (.a(xor_2_out), .b(8'h1), .c_i(1'b0), .s(add_6_s));  // open: c_o
  Register #(.Bits(8)) register_1 (.D(multiplexer_2_out), .C(clk), .en(result1_0), .Q(out_21));
  Register #(.Bits(8)) register_2 (.D(multiplexer_3_out), .C(clk), .en(reset1_0), .Q(out_14));
  Comparator #(.Bits(8)) comparator_1 (.a(K), .b(8'hf), .lt(comparator_1_lt));  // open: gt, eq
  Register #(.Bits(8)) register_3 (.D(multiplexer_1_out), .C(clk), .en(or_2_out), .Q(K));
  Multiplexer #(.Bits(8)) multiplexer_4 (.sel(accA[7]), .in_0(accA), .in_1(add_5_s), .out(_2_comA));
  Multiplexer #(.Bits(8)) multiplexer_5 (.sel(accB[7]), .in_0(accB), .in_1(add_6_s), .out(_2_comB));
  Multiplexer #(.Bits(8)) multiplexer_6 (.sel(comparator_1_lt), .in_0(K), .in_1(8'hf), .out(multiplexer_6_out));
  or or_3 (or_3_out, _12, and_1_out, and_2_out, and_3_out, and_4_out);
  Comparator #(.Bits(8)) comparator_2 (.a(out_21), .b(8'hf), .eq(Done_t));  // open: gt, lt
  Comparator #(.Bits(8)) comparator_3 (.a(out_14), .b(multiplexer_6_out), .eq(comparator_3_eq));  // open: gt, lt
  not not_1 (not_1_out, Done_t);
  not not_2 (not_2_out, comparator_3_eq);
  Multiplexer #(.Selector_Bits(2), .Bits(8)) multiplexer_7 (
    .sel({accB[7], accA[7]}), .in_0(_2_comA_2_comB), .in_1(_2_com_2_comA_plus_2_comB),
    .in_2(_2_comA_plus_2_comB), .in_3(_2_comB_2_comA), .out(A_B));
  Multiplexer #(.Selector_Bits(2), .Bits(8)) multiplexer_8 (
    .sel({accB[7], accA[7]}), .in_0(_2_comA_plus_2_comB), .in_1(_2_comB_2_comA), .in_2(_2_comA_2_comB),
    .in_3(_2_com_2_comA_plus_2_comB), .out(A_plus_B));
  Add #(.Bits(8)) add_7 (.a(out_15), .b(8'h1), .c_i(1'b0), .s(add_7_s));  // open: c_o
  Multiplexer #(.Bits(8)) multiplexer_9 (
    .sel(or_3_out), .in_0(multiplexer_10_out), .in_1(Operand), .out(multiplexer_9_out));
  and and_5 (and_5_out, not_1_out, d_ff_1_q);
  and and_6 (and_6_out, not_1_out, result, ~d_ff_1_q);  // And
  and and_7 (and_7_out, not_2_out, d_ff_2_q);
  and and_8 (and_8_out, not_2_out, reset, ~d_ff_2_q);  // And
  Multiplexer #(.Bits(8)) multiplexer_10 (.sel(startread1), .in_0({8{1'b0}}), .in_1(add_7_s), .out(multiplexer_10_out));
  Register #(.Bits(8)) register_4 (.D(multiplexer_9_out), .C(clk), .en(startread1_0), .Q(out_15));
  assign xor_3_out = _2_comA_plus_2_comB ^ {8{1'b1}};  // XOr xor_3, 8 bits wide
  assign xor_4_out = _2_comB_2_comA ^ {8{1'b1}};  // XOr xor_4, 8 bits wide
  assign xor_5_out = _2_comA_2_comB ^ {8{1'b1}};  // XOr xor_5, 8 bits wide
  or or_4 (or_4_out, and_5_out, and_6_out);
  or or_5 (or_5_out, and_7_out, and_8_out);
  Decoder #(.Selector_Bits(5)) decoder_1 (
    .sel(out_16), .out_0(_0), .out_1(_1), .out_2(_2), .out_3(_3), .out_4(_4), .out_5(_5), .out_6(_6),
    .out_7(_7), .out_8(_8), .out_9(_9), .out_10(_10), .out_11(_11), .out_12(_12), .out_13(_13), .out_14(_14),
    .out_15(_15), .out_16(_16), .out_17(_17), .out_18(_18), .out_19(_19), .out_20(_20), .out_21(_21),
    .out_22(_22), .out_23(_23), .out_24(_24), .out_25(_25), .out_26(_26), .out_27(_27), .out_28(_28),
    .out_29(_29), .out_30(_30_t), .out_31(_31));
  Add #(.Bits(8)) add_8 (.a(xor_3_out), .b(8'h1), .c_i(1'b0), .s(_2_com_2_comA_plus_2_comB));  // open: c_o
  Add #(.Bits(8)) add_9 (.a(xor_4_out), .b(8'h1), .c_i(1'b0), .s(_2_com_2_comB_2_comA));  // open: c_o
  Add #(.Bits(8)) add_10 (.a(xor_5_out), .b(8'h1), .c_i(1'b0), .s(_2_com_2_comA_2_comB));  // open: c_o
  D_FF d_ff_1 (.D(or_4_out), .C(clk), .Q(d_ff_1_q));  // open: nQ
  D_FF d_ff_2 (.D(or_5_out), .C(clk), .Q(d_ff_2_q));  // open: nQ
  Decoder decoder_2 (.sel(d_ff_1_q), .out_0(result0), .out_1(result1));
  Decoder decoder_3 (.sel(d_ff_2_q), .out_0(reset0), .out_1(reset1));
  Decoder decoder_4 (.sel(d_ff_3_q), .out_0(startread0), .out_1(startread1));
  and and_9 (and_9_out, ~reset, or_9_out);  // And
  and and_10 (and_10_out, ~d_ff_3_q, start);  // And
  and and_11 (and_11_out, d_ff_3_q, ~_31);  // And
  Comparator #(.Bits(8)) comparator_4 (
    .a(_2_comA), .b(_2_comB), .gt(comparator_4_gt), .eq(comparator_4_eq), .lt(comparator_4_lt));
  or or_6 (result1_0, result0, result1);
  or or_7 (reset1_0, reset0, reset1);
  or or_8 (startread1_0, startread0, startread1);
  D_FF d_ff_3 (.D(and_9_out), .C(clk), .Q(d_ff_3_q));  // open: nQ
  or or_9 (or_9_out, and_10_out, and_11_out);
  Multiplexer #(.Selector_Bits(2)) multiplexer_11 (
    .sel({accB[7], accA[7]}), .in_0(comparator_4_eq), .in_1(1'b0), .in_2(1'b0), .in_3(comparator_4_eq),
    .out(multiplexer_11_out));
  Multiplexer #(.Selector_Bits(2)) multiplexer_12 (
    .sel({accB[7], accA[7]}), .in_0(comparator_4_lt), .in_1(1'b1), .in_2(1'b0), .in_3(comparator_4_gt),
    .out(multiplexer_12_out));
  Multiplexer #(.Selector_Bits(2)) multiplexer_13 (
    .sel({accB[7], accA[7]}), .in_0(comparator_4_gt), .in_1(1'b0), .in_2(1'b1), .in_3(comparator_4_lt),
    .out(multiplexer_13_out));
  Multiplexer multiplexer_14 (.sel(_23), .in_0(1'b0), .in_1(multiplexer_11_out), .out(multiplexer_14_out));
  ROM #(.AddrBits(8)) rom_1 (.A(accA), .sel(1'b1), .D(rom_1_d));
  Multiplexer #(.Bits(8)) multiplexer_15 (.sel(progLoad), .in_0(out_14), .in_1(K), .out(multiplexer_15_out));
  Multiplexer #(.Bits(13)) multiplexer_16 (.sel(progLoad), .in_0({13{1'b0}}), .in_1(progIN), .out(multiplexer_16_out));
  Multiplexer #(.Bits(8)) multiplexer_17 (.sel(_9), .in_0(Address1), .in_1(Operand), .out(AddressOperand1));
  Multiplexer multiplexer_18 (.sel(_23), .in_0(1'b0), .in_1(multiplexer_12_out), .out(multiplexer_18_out));
  Multiplexer multiplexer_19 (.sel(_23), .in_0(1'b0), .in_1(multiplexer_13_out), .out(multiplexer_19_out));
  Multiplexer multiplexer_20 (.sel(_29), .in_0(multiplexer_14_out), .in_1(rom_1_d), .out(multiplexer_20_out));
  or or_10 (or_10_out, _29, _23);
  Register register_5 (.D(multiplexer_18_out), .C(clk), .en(_23), .Q(lesser));
  Register register_6 (.D(multiplexer_19_out), .C(clk), .en(_23), .Q(greater));
  Register register_7 (.D(multiplexer_20_out), .C(clk), .en(or_10_out), .Q(equal));
  Multiplexer #(.Bits(8)) multiplexer_21 (.sel(startread1), .in_0(multiplexer_15_out), .in_1(out_15), .out(Address1));
  Multiplexer #(.Bits(13)) multiplexer_22 (
    .sel(startread1), .in_0(multiplexer_16_out), .in_1({out_16, Operand}), .out(Value1));
  or or_11 (or_11_out, _11, or_12_out, reset1);
  or or_12 (or_12_out, counter1, counter2);
  Div #(.Bits(8)) div_1 (.a(accA), .b(accB), .q(div_1_q), .r(div_1_r));
  Multiplexer #(.Bits(8)) multiplexer_23 (
    .sel(_20), .in_0(multiplexer_49_out), .in_1(div_1_q), .out(multiplexer_23_out));
  ROM #(.AddrBits(6), .Bits(8)) rom_2 (.A({accA[2:0], accB[2:0]}), .sel(1'b1), .D(rom_2_d));
  RAMDualAccess #(.AddrBits(8), .Bits(13)) pRAM (
    .str(progLoad), .C(clk), .ld(startread1), .A1(Address1), .Din1(Value1), .A2(AddressOperand1),
    .D1(pRAM_d1), .D2(out_13));
  RAMDualAccess #(.AddrBits(8), .Bits(8)) rRAM (
    .str(or_11_out), .C(clk), .ld(_30_t), .A1(Address2), .Din1(Value2), .A2(AddressOperand2),
    .D1(ReadValue2), .D2(out_20));
  Multiplexer #(.Bits(8)) multiplexer_24 (.sel(_1), .in_0({8{1'b0}}), .in_1(Operand), .out(multiplexer_24_out));
  Multiplexer #(.Bits(8)) multiplexer_25 (
    .sel(_21), .in_0(multiplexer_23_out), .in_1(div_1_r), .out(multiplexer_25_out));
  Multiplexer #(.Bits(8)) multiplexer_26 (.sel(_11), .in_0({8{1'b0}}), .in_1(accA), .out(multiplexer_26_out));
  Multiplexer #(.Bits(8)) multiplexer_27 (.sel(_3), .in_0(multiplexer_24_out), .in_1(accB), .out(multiplexer_27_out));
  Multiplexer #(.Bits(8)) multiplexer_28 (
    .sel(_22), .in_0(multiplexer_25_out), .in_1(rom_2_d), .out(multiplexer_28_out));
  assign xor_6_out = accA ^ {8{1'b1}};  // XOr xor_6, 8 bits wide
  Sub #(.Bits(8)) sub_3 (.a(register_8_q), .b(register_9_q), .c_i(1'b0), .s(sub_3_s));  // open: c_o
  Sub #(.Bits(8)) sub_4 (.a(register_9_q), .b(register_8_q), .c_i(1'b0), .s(sub_4_s));  // open: c_o
  Multiplexer #(.Bits(8)) multiplexer_29 (.sel(result1), .in_0(Operand), .in_1(out_21), .out(multiplexer_29_out));
  Multiplexer #(.Bits(8)) multiplexer_30 (
    .sel(counter1), .in_0(multiplexer_26_out), .in_1(lcm[7:0]), .out(multiplexer_30_out));
  Multiplexer #(.Bits(13)) multiplexer_31 (
    .sel(startread1), .in_0({13{1'b0}}), .in_1(pRAM_d1), .out({out_16, Operand}));
  Multiplexer #(.Bits(8)) multiplexer_32 (.sel(result1), .in_0({8{1'b0}}), .in_1(out_20), .out(\output ));
  Multiplexer #(.Bits(8)) multiplexer_33 (.sel(_6), .in_0(multiplexer_27_out), .in_1(regC), .out(multiplexer_33_out));
  Multiplexer #(.Bits(8)) multiplexer_34 (
    .sel(_24), .in_0(multiplexer_28_out), .in_1(xor_6_out), .out(multiplexer_34_out));
  assign and_12_out = accA & accB;  // And and_12, 8 bits wide
  Multiplexer #(.Bits(8)) multiplexer_35 (
    .sel(decoder_5_out_3), .in_0(out_20), .in_1(sub_3_s), .out(multiplexer_35_out));
  Multiplexer #(.Bits(8)) multiplexer_36 (
    .sel(decoder_5_out_2), .in_0(ReadValue2), .in_1(sub_4_s), .out(multiplexer_36_out));
  Multiplexer #(.Bits(8)) multiplexer_37 (
    .sel(reset1), .in_0(multiplexer_29_out), .in_1(out_14), .out(multiplexer_37_out));
  Multiplexer #(.Bits(8)) multiplexer_38 (.sel(counter2), .in_0(multiplexer_30_out), .in_1(lcm[15:8]), .out(Value2));
  Seven_Seg_Hex seven_seg_hex_1 (.d(\output [7:4]), .dp(1'b0));
  or or_13 (or_13_out, Done_t, reset, start, result);
  or or_14 (or_14_out, reset, start, _31);
  Multiplexer #(.Bits(8)) multiplexer_39 (
    .sel(_9), .in_0(multiplexer_33_out), .in_1(out_13[7:0]), .out(multiplexer_39_out));
  Multiplexer #(.Bits(8)) multiplexer_40 (
    .sel(_25), .in_0(multiplexer_34_out), .in_1(and_12_out), .out(multiplexer_40_out));
  assign or_15_out = accA | accB;  // Or or_15, 8 bits wide
  Register #(.Bits(8)) register_8 (.D(multiplexer_35_out), .C(clk), .en(or_20_out), .Q(register_8_q));
  Register #(.Bits(8)) register_9 (.D(multiplexer_36_out), .C(clk), .en(or_21_out), .Q(register_9_q));
  Register register_10 (.D(Done_t), .C(clk), .en(or_13_out), .Q(done));
  Register register_11 (.D(_31), .C(clk), .en(or_14_out), .Q(valid));
  Multiplexer #(.Bits(8)) multiplexer_41 (
    .sel(_10), .in_0(multiplexer_39_out), .in_1(out_20), .out(multiplexer_41_out));
  Multiplexer #(.Bits(8)) multiplexer_42 (
    .sel(_26), .in_0(multiplexer_40_out), .in_1(or_15_out), .out(multiplexer_42_out));
  assign xor_7_out = accA ^ accB;  // XOr xor_7, 8 bits wide
  Seven_Seg_Hex seven_seg_hex_2 (.d(\output [3:0]), .dp(1'b0));
  Multiplexer #(.Bits(8)) multiplexer_43 (
    .sel(_17), .in_0(multiplexer_41_out), .in_1(A_plus_B), .out(multiplexer_43_out));
  Comparator #(.Bits(8)) comparator_5 (
    .a(register_8_q), .b(register_9_q), .gt(comparator_5_gt), .eq(comparator_5_eq));  // open: lt
  Multiplexer #(.Bits(8)) multiplexer_44 (
    .sel(_30_t), .in_0(multiplexer_37_out), .in_1({4'b0000, Operand[3:0]}), .out(AddressOperand2));
  Multiplexer #(.Bits(8)) multiplexer_45 (.sel(_18), .in_0(multiplexer_43_out), .in_1(A_B), .out(multiplexer_45_out));
  Mul #(.Bits(4)) mul_1 (.a(accA[3:0]), .b(accB[3:0]), .mul(mul_1_mul));
  Multiplexer #(.Bits(8)) multiplexer_46 (
    .sel(_27), .in_0(multiplexer_42_out), .in_1(xor_7_out), .out(multiplexer_46_out));
  and and_13 (and_13_out, comparator_5_gt, ~comparator_5_eq);  // And
  and and_14 (and_14_out, ~comparator_5_gt, ~comparator_5_eq);  // And
  Multiplexer #(.Bits(8)) multiplexer_47 (.sel(_5), .in_0({8{1'b0}}), .in_1(accA), .out(multiplexer_47_out));
  Multiplexer #(.Bits(8)) multiplexer_48 (.sel(_2), .in_0({8{1'b0}}), .in_1(Operand), .out(multiplexer_48_out));
  Multiplexer #(.Bits(8)) multiplexer_49 (
    .sel(_19), .in_0(multiplexer_45_out), .in_1(mul_1_mul), .out(multiplexer_49_out));
  Multiplexer #(.Bits(8)) multiplexer_50 (
    .sel(_28), .in_0(multiplexer_46_out), .in_1(barrelshifter_1_out), .out(multiplexer_50_out));
  BarrelShifter #(.Bits(8)) barrelshifter_1 (.in(accA), .shift({1'b0, accB[2:0]}), .out(barrelshifter_1_out));
  and and_15 (and_15_out, comparator_5_gt, ~comparator_5_eq);  // And
  Multiplexer #(.Bits(8)) multiplexer_51 (.sel(_11), .in_0(Operand), .in_1(Operand), .out(multiplexer_51_out));
  Multiplexer #(.Bits(8)) multiplexer_52 (.sel(_7), .in_0(multiplexer_47_out), .in_1(M), .out(multiplexer_52_out));
  or or_16 (or_16_out, and_13_out, and_14_out);
  Multiplexer #(.Bits(8)) multiplexer_53 (
    .sel(_30_t), .in_0(multiplexer_51_out), .in_1({4'b0000, Operand[7:4]}), .out(multiplexer_53_out));
  Multiplexer #(.Bits(8)) multiplexer_54 (.sel(_8), .in_0(multiplexer_52_out), .in_1(N), .out(multiplexer_54_out));
  Multiplexer #(.Bits(8)) multiplexer_55 (.sel(_4), .in_0(multiplexer_48_out), .in_1(accA), .out(multiplexer_55_out));
  or or_17 (or_17_out, _2, reset, _4);
  or or_18 (or_18_out, _1, _3, _6, _9, _10, _17, _18, _19, reset, _20, _21, _22, _24, _25, _26, _27, _28);
  Multiplexer #(.Selector_Bits(2)) multiplexer_56 (
    .sel(d_ff_4_q), .in_0(_30_t), .in_1(and_15_out), .in_2(1'b1), .in_3(1'b1), .out(multiplexer_56_out));
  Multiplexer #(.Bits(8)) multiplexer_57 (
    .sel(counter1), .in_0(multiplexer_53_out), .in_1(8'hf), .out(multiplexer_57_out));
  or or_19 (or_19_out, _5, _7, _8, reset);
  Register #(.Bits(8)) register_12 (.D(multiplexer_55_out), .C(clk), .en(or_17_out), .Q(accB));
  Register #(.Bits(8)) register_13 (.D(multiplexer_50_out), .C(clk), .en(or_18_out), .Q(accA));
  Multiplexer #(.Selector_Bits(2)) multiplexer_58 (
    .sel(d_ff_4_q), .in_0(1'b0), .in_1(or_16_out), .in_2(1'b0), .in_3(1'b0), .out(multiplexer_58_out));
  Multiplexer #(.Bits(8)) multiplexer_59 (.sel(counter2), .in_0(multiplexer_57_out), .in_1(8'he), .out(Address2));
  Register #(.Bits(8)) register_14 (.D(multiplexer_54_out), .C(clk), .en(or_19_out), .Q(regC));
  and and_16 (and_16_out, 1'b1, multiplexer_58_out);
  and and_17 (and_17_out, 1'b1, multiplexer_56_out);
  D_FF d_ff_4 (.D(and_16_out), .C(clk), .Q(d_ff_4_q[1]));  // open: nQ
  D_FF d_ff_5 (.D(and_17_out), .C(clk), .Q(d_ff_4_q[0]));  // open: nQ
  Decoder #(.Selector_Bits(2)) decoder_5 (
    .sel(d_ff_4_q), .out_0(decoder_5_out_0), .out_1(decoder_5_out_1), .out_2(decoder_5_out_2),
    .out_3(decoder_5_out_3));
  or or_20 (or_20_out, decoder_5_out_0, decoder_5_out_3);
  or or_21 (or_21_out, decoder_5_out_0, decoder_5_out_2);
  not not_3 (out_25, decoder_5_out_0);
  Register #(.Bits(8)) register_15 (.D(register_8_q), .C(clk), .en(decoder_5_out_1), .Q(gcd));
  Register #(.Bits(8)) register_16 (.D(out_20), .C(clk), .en(_30_t), .Q(register_16_q));
  Register #(.Bits(8)) register_17 (.D(ReadValue2), .C(clk), .en(_30_t), .Q(register_17_q));
  Mul #(.Bits(8)) mul_2 (.a(register_16_q), .b(register_17_q), .mul(mul_2_mul));
  Div #(.Bits(16)) div_2 (.a(mul_2_mul), .b({{8{1'b0}}, gcd}), .q(div_2_q));  // open: r
  Register register_18 (.D(_30_t), .C(clk), .en(_30_t), .Q(register_18_q));
  D_FF #(.Bits(16)) d_ff_6 (.D(div_2_q), .C(clk), .Q(lcm));  // open: nQ
  and and_18 (_30, register_18_q, ~out_25);  // And
  Counter #(.Bits(2)) counter_1 (.en(_30), .C(clk), .clr(1'b0), .out(counter_1_out));  // open: ovf
  Decoder #(.Selector_Bits(2)) decoder_6 (
    .sel(counter_1_out), .out_0(counter0), .out_1(counter1), .out_2(counter2), .out_3(counter3));

  // Other names for the same wires on the sheet: busy = out_25; haved30 = _30; ReadAddress[7:0] = out_15;
  //   ReadAddressOperand1[12:0] = out_13; ReadAddressOperand2[7:0] = out_20; ReadValue1[12:0] = {out_16, Operand};
  //   ResetAddress[7:0] = out_14; ResultAddress[7:0] = out_21; StartRead = start; StartWrite = progLoad;
  //   WriteAddress[7:0] = K; WriteValue[12:0] = progIN

  // Notes on the sheet:
  //   progIN: default 1
  //   Result
  //   Reset
  //   Write
  //   Jump
  //   CO-OP999
  //   6733185821 Penpitcha Piyawaranont
  //   6733255021 Sirikarn Fugsrimuang
  //   6733284221 Atipat Buranavatanachoke
  //   6733293921 Aitsayaphan Limmuangnil
  //   2's complement
  //   Read
  //   Greater Lesser Equal
  //   Write Adress and Value RAM1
  //   0-reset 1-write
  //   contents of rom_1 (hex, n*v repeats v):
  //   0,0,1,1,0,1,0,1,0,a,a,1,a,1,a,a,0,1,4,1,10,20,40,1,0,4*a,1,0,1
  //   ,0,4,10,40,0,1,0,0,0,1,a,1,0,0,0,1,0,6,24,d8,0,1,0,0,0,a,a,1,0
  //   ,1,5*0,1,0,0,0,1,0,1,5*0,1,0,0,0,1,5*0,1,7*0,1,0,0,0,1,0,1,0,0,0
  //   ,b,0,1,0,0,0,1,13*0,1,0,0,0,1,5*0,1,0,1,9*0,1,0,1,5*0,1,5*0,1
  //   ,0,0,0,1,5*0,1,5*0,1,0,1,9*0,1,0,1,0,0,0,1,0,1,11*0,1,11*0,1,0,0,0
  //   ,1,0,1,0,0,0,1,5*0,1,0,1,9*0,1
  //   1-read
  //   A
  //   contents of rom_2 (hex, n*v repeats v):
  //   1,7*0,9*1,2,4,8,10,20,40,80,1,3,9,1b,51,f3,d9,8b,1,4,10,40,4*0
  //   ,1,5,19,7d,71,35,9,2d,1,6,24,d8,10,60,40,80,1,7,31,57,61,a7,91,f7
  //   Write Adress and Value RAM2
  //   0-writeOperand
  //   1-result
  //   a
  //   b
  //   ag
  //   eg
  //   C
  //   B
  //   AllTask
  //   Qa
  //   Qb
  //   setb
  //   seta
  //   loadA
  //   loadB
endmodule

/* Test case 01_P01T01:
M N progIN reset progLoad start result clk valid done output
0 0 0 0 0 0 0 0 0 0 0
0 0 0 0 0 0 0 1 0 0 0
0 0 0 1 0 0 0 0 0 0 0
0 0 0 1 0 0 0 1 0 0 0
0 0 0 0 0 0 0 0 0 0 0
0 0 0 0 0 0 0 1 0 0 0
0 0 0 0 0 0 0 0 0 0 0
0 0 0 0 0 0 0 1 0 0 0
0 0 0 0 0 0 0 0 0 0 0
0 0 0 0 0 0 0 1 0 0 0
0 0 0 0 0 0 0 0 0 0 0
0 0 0 0 0 0 0 1 0 0 0
0 0 0 0 0 0 0 0 0 0 0
0 0 0 0 0 0 0 1 0 0 0
0 0 0 0 0 0 0 0 0 0 0
0 0 0 0 0 0 0 1 0 0 0
0 0 0 0 0 0 0 0 0 0 0
0 0 0 0 0 0 0 1 0 0 0
0 0 0 0 0 0 0 0 0 0 0
0 0 0 0 0 0 0 1 0 0 0
0 0 0 0 0 0 0 0 0 0 0
0 0 0 0 0 0 0 1 0 0 0
0 0 0 0 0 0 0 0 0 0 0
0 0 0 0 0 0 0 1 0 0 0
0 0 0 0 0 0 0 0 0 0 0
0 0 0 0 0 0 0 1 0 0 0
0 0 0 0 0 0 0 0 0 0 0
0 0 0 0 0 0 0 1 0 0 0
0 0 0 0 0 0 0 0 0 0 0
0 0 0 0 0 0 0 1 0 0 0
0 0 0 0 0 0 0 0 0 0 0
0 0 0 0 0 0 0 1 0 0 0
0 0 0 0 0 0 0 0 0 0 0
0 0 0 0 0 0 0 1 0 0 0
0 0 0 0 0 0 0 0 0 0 0
0 0 0 0 0 0 0 1 0 0 0
0 0 0 0 0 0 0 0 0 0 0
0 0 0 0 0 0 0 1 0 0 0
0 0 0 0 0 0 0 0 0 0 0
0 0 0 0 0 0 0 1 0 0 0
0 0 0 0 0 0 0 0 0 0 0
0 0 0 0 0 0 0 1 0 0 0
0 0 271 0 1 0 0 0 0 0 0
0 0 0 0 1 0 0 1 0 0 0
0 0 565 0 1 0 0 0 0 0 0
0 0 0 0 1 0 0 1 0 0 0
0 0 4352 0 1 0 0 0 0 0 0
0 0 0 0 1 0 0 1 0 0 0
0 0 2819 0 1 0 0 0 0 0 0
0 0 0 0 1 0 0 1 0 0 0
0 0 7936 0 1 0 0 0 0 0 0
0 0 0 0 1 0 0 1 0 0 0
0 0 0 0 0 1 0 0 0 0 0
0 0 0 0 0 1 0 1 0 0 0
0 0 0 0 0 0 0 0 x 0 0
0 0 0 0 0 0 0 1 x 0 0
0 0 0 0 0 0 0 0 x 0 0
0 0 0 0 0 0 0 1 x 0 0
0 0 0 0 0 0 0 0 x 0 0
0 0 0 0 0 0 0 1 x 0 0
0 0 0 0 0 0 0 0 x 0 0
0 0 0 0 0 0 0 1 x 0 0
0 0 0 0 0 0 0 0 x 0 0
0 0 0 0 0 0 0 1 x 0 0
0 0 0 0 0 0 0 0 x 0 0
0 0 0 0 0 0 0 1 x 0 0
0 0 0 0 0 0 0 0 x 0 0
0 0 0 0 0 0 0 1 x 0 0
0 0 0 0 0 0 0 0 x 0 0
0 0 0 0 0 0 0 1 x 0 0
0 0 0 0 0 0 0 0 x 0 0
0 0 0 0 0 0 0 1 x 0 0
0 0 0 0 0 0 0 0 x 0 0
0 0 0 0 0 0 0 1 x 0 0
0 0 0 0 0 0 0 0 x 0 0
0 0 0 0 0 0 0 1 x 0 0
0 0 0 0 0 0 0 0 x 0 0
0 0 0 0 0 0 0 1 x 0 0
0 0 0 0 0 0 0 0 x 0 0
0 0 0 0 0 0 0 1 x 0 0
0 0 0 0 0 0 0 0 x 0 0
0 0 0 0 0 0 0 1 x 0 0
0 0 0 0 0 0 0 0 x 0 0
0 0 0 0 0 0 0 1 x 0 0
0 0 0 0 0 0 0 0 x 0 0
0 0 0 0 0 0 0 1 x 0 0
0 0 0 0 0 0 0 0 x 0 0
0 0 0 0 0 0 0 1 x 0 0
0 0 0 0 0 0 0 0 x 0 0
0 0 0 0 0 0 0 1 x 0 0
0 0 0 0 0 0 0 0 x 0 0
0 0 0 0 0 0 0 1 x 0 0
0 0 0 0 0 0 0 0 x 0 0
0 0 0 0 0 0 0 1 x 0 0
0 0 0 0 0 0 0 0 x 0 0
0 0 0 0 0 0 0 1 x 0 0
0 0 0 0 0 0 0 0 x 0 0
0 0 0 0 0 0 0 1 x 0 0
0 0 0 0 0 0 0 0 x 0 0
0 0 0 0 0 0 0 1 x 0 0
0 0 0 0 0 0 0 0 x 0 0
0 0 0 0 0 0 0 1 x 0 0
0 0 0 0 0 0 0 0 x 0 0
0 0 0 0 0 0 0 1 x 0 0
0 0 0 0 0 0 0 0 x 0 0
0 0 0 0 0 0 0 1 1 0 0
0 0 0 0 0 0 1 0 1 0 0
0 0 0 0 0 0 1 1 1 0 0
0 0 0 0 0 0 0 0 1 0 0
0 0 0 0 0 0 0 1 1 0 0
0 0 0 0 0 0 0 0 1 0 0
0 0 0 0 0 0 0 1 1 0 0
0 0 0 0 0 0 0 0 1 0 0
0 0 0 0 0 0 0 1 1 0 68
0 0 0 0 0 0 0 0 1 0 68
0 0 0 0 0 0 0 1 1 0 0
0 0 0 0 0 0 0 0 1 0 0
0 0 0 0 0 0 0 1 1 0 0
0 0 0 0 0 0 0 0 1 0 0
0 0 0 0 0 0 0 1 1 0 0
0 0 0 0 0 0 0 0 1 0 0
0 0 0 0 0 0 0 1 1 0 0
0 0 0 0 0 0 0 0 1 0 0
0 0 0 0 0 0 0 1 1 0 0
0 0 0 0 0 0 0 0 1 0 0
0 0 0 0 0 0 0 1 1 0 0
0 0 0 0 0 0 0 0 1 0 0
0 0 0 0 0 0 0 1 1 0 0
0 0 0 0 0 0 0 0 1 0 0
0 0 0 0 0 0 0 1 1 0 0
0 0 0 0 0 0 0 0 1 0 0
0 0 0 0 0 0 0 1 1 0 0
0 0 0 0 0 0 0 0 1 0 0
0 0 0 0 0 0 0 1 1 0 0
0 0 0 0 0 0 0 0 1 0 0
0 0 0 0 0 0 0 1 1 0 0
0 0 0 0 0 0 0 0 1 0 0
0 0 0 0 0 0 0 1 1 0 0
0 0 0 0 0 0 0 0 1 0 0
0 0 0 0 0 0 0 1 1 1 0
0 0 0 0 0 0 0 0 1 1 0
0 0 0 0 0 0 0 1 1 1 0
0 0 0 0 0 0 0 0 1 1 0
*/

/* Test case 02_P01T02:
M N progIN reset progLoad start result clk valid done output
0 0 0 0 0 0 0 0 x x x
0 0 0 0 0 0 0 1 x x x
0 0 0 1 0 0 0 0 x x x
0 0 0 1 0 0 0 1 0 0 x
0 0 0 0 0 0 0 0 0 0 x
0 0 0 0 0 0 0 1 0 0 x
0 0 0 0 0 0 0 0 0 0 x
0 0 0 0 0 0 0 1 0 0 x
0 0 0 0 0 0 0 0 0 0 x
0 0 0 0 0 0 0 1 0 0 x
0 0 0 0 0 0 0 0 0 0 x
0 0 0 0 0 0 0 1 0 0 x
0 0 0 0 0 0 0 0 0 0 x
0 0 0 0 0 0 0 1 0 0 x
0 0 0 0 0 0 0 0 0 0 x
0 0 0 0 0 0 0 1 0 0 x
0 0 0 0 0 0 0 0 0 0 x
0 0 0 0 0 0 0 1 0 0 x
0 0 0 0 0 0 0 0 0 0 x
0 0 0 0 0 0 0 1 0 0 x
0 0 0 0 0 0 0 0 0 0 x
0 0 0 0 0 0 0 1 0 0 x
0 0 0 0 0 0 0 0 0 0 x
0 0 0 0 0 0 0 1 0 0 x
0 0 0 0 0 0 0 0 0 0 x
0 0 0 0 0 0 0 1 0 0 x
0 0 0 0 0 0 0 0 0 0 x
0 0 0 0 0 0 0 1 0 0 x
0 0 0 0 0 0 0 0 0 0 x
0 0 0 0 0 0 0 1 0 0 x
0 0 0 0 0 0 0 0 0 0 x
0 0 0 0 0 0 0 1 0 0 x
0 0 0 0 0 0 0 0 0 0 x
0 0 0 0 0 0 0 1 0 0 x
0 0 0 0 0 0 0 0 0 0 x
0 0 0 0 0 0 0 1 0 0 x
0 0 0 0 0 0 0 0 0 0 x
0 0 0 0 0 0 0 1 0 0 x
0 0 0 0 0 0 0 0 0 0 x
0 0 0 0 0 0 0 1 0 0 x
0 0 0 0 0 0 0 0 0 0 x
0 0 0 0 0 0 0 1 0 0 x
0 0 271 0 1 0 0 0 0 0 x
0 0 271 0 1 0 0 1 0 0 x
0 0 565 0 1 0 0 0 0 0 x
0 0 565 0 1 0 0 1 0 0 x
0 0 4352 0 1 0 0 0 0 0 x
0 0 4352 0 1 0 0 1 0 0 x
0 0 2819 0 1 0 0 0 0 0 x
0 0 2819 0 1 0 0 1 0 0 x
0 0 7936 0 1 0 0 0 0 0 x
0 0 7936 0 1 0 0 1 0 0 x
0 0 0 0 0 1 0 0 0 0 x
0 0 0 0 0 1 0 1 0 0 x
0 0 0 0 0 0 0 0 x 0 x
0 0 0 0 0 0 0 1 x 0 x
0 0 0 0 0 0 0 0 x 0 x
0 0 0 0 0 0 0 1 x 0 x
0 0 0 0 0 0 0 0 x 0 x
0 0 0 0 0 0 0 1 x 0 x
0 0 0 0 0 0 0 0 x 0 x
0 0 0 0 0 0 0 1 x 0 x
0 0 0 0 0 0 0 0 x 0 x
0 0 0 0 0 0 0 1 x 0 x
0 0 0 0 0 0 0 0 x 0 x
0 0 0 0 0 0 0 1 x 0 x
0 0 0 0 0 0 0 0 x 0 x
0 0 0 0 0 0 0 1 x 0 x
0 0 0 0 0 0 0 0 x 0 x
0 0 0 0 0 0 0 1 x 0 x
0 0 0 0 0 0 0 0 x 0 x
0 0 0 0 0 0 0 1 x 0 x
0 0 0 0 0 0 0 0 x 0 x
0 0 0 0 0 0 0 1 x 0 x
0 0 0 0 0 0 0 0 x 0 x
0 0 0 0 0 0 0 1 x 0 x
0 0 0 0 0 0 0 0 x 0 x
0 0 0 0 0 0 0 1 x 0 x
0 0 0 0 0 0 0 0 x 0 x
0 0 0 0 0 0 0 1 x 0 x
0 0 0 0 0 0 0 0 x 0 x
0 0 0 0 0 0 0 1 x 0 x
0 0 0 0 0 0 0 0 x 0 x
0 0 0 0 0 0 0 1 x 0 x
0 0 0 0 0 0 0 0 x 0 x
0 0 0 0 0 0 0 1 x 0 x
0 0 0 0 0 0 0 0 x 0 x
0 0 0 0 0 0 0 1 x 0 x
0 0 0 0 0 0 0 0 x 0 x
0 0 0 0 0 0 0 1 x 0 x
0 0 0 0 0 0 0 0 x 0 x
0 0 0 0 0 0 0 1 x 0 x
0 0 0 0 0 0 0 0 x 0 x
0 0 0 0 0 0 0 1 x 0 x
0 0 0 0 0 0 0 0 x 0 x
0 0 0 0 0 0 0 1 x 0 x
0 0 0 0 0 0 0 0 x 0 x
0 0 0 0 0 0 0 1 x 0 x
0 0 0 0 0 0 0 0 x 0 x
0 0 0 0 0 0 0 1 x 0 x
0 0 0 0 0 0 0 0 x 0 x
0 0 0 0 0 0 0 1 x 0 x
0 0 0 0 0 0 0 0 x 0 x
0 0 0 0 0 0 0 1 x 0 x
0 0 0 0 0 0 0 0 x 0 x
0 0 0 0 0 0 0 1 1 0 x
0 0 0 0 0 0 1 0 1 0 x
0 0 0 0 0 0 1 1 1 0 0
0 0 0 0 0 0 0 0 1 0 0
0 0 0 0 0 0 0 1 1 0 0
0 0 0 0 0 0 0 0 1 0 0
0 0 0 0 0 0 0 1 1 0 0
0 0 0 0 0 0 0 0 1 0 0
0 0 0 0 0 0 0 1 1 0 68
0 0 0 0 0 0 0 0 1 0 68
0 0 0 0 0 0 0 1 1 0 0
0 0 0 0 0 0 0 0 1 0 0
0 0 0 0 0 0 0 1 1 0 0
0 0 0 0 0 0 0 0 1 0 0
0 0 0 0 0 0 0 1 1 0 0
0 0 0 0 0 0 0 0 1 0 0
0 0 0 0 0 0 0 1 1 0 0
0 0 0 0 0 0 0 0 1 0 0
0 0 0 0 0 0 0 1 1 0 0
0 0 0 0 0 0 0 0 1 0 0
0 0 0 0 0 0 0 1 1 0 0
0 0 0 0 0 0 0 0 1 0 0
0 0 0 0 0 0 0 1 1 0 0
0 0 0 0 0 0 0 0 1 0 0
0 0 0 0 0 0 0 1 1 0 0
0 0 0 0 0 0 0 0 1 0 0
0 0 0 0 0 0 0 1 1 0 0
0 0 0 0 0 0 0 0 1 0 0
0 0 0 0 0 0 0 1 1 0 0
0 0 0 0 0 0 0 0 1 0 0
0 0 0 0 0 0 0 1 1 0 0
0 0 0 0 0 0 0 0 1 0 0
0 0 0 0 0 0 0 1 1 0 0
0 0 0 0 0 0 0 0 1 0 0
0 0 0 0 0 0 0 1 1 1 x
0 0 0 0 0 0 0 0 1 1 x
0 0 0 0 0 0 0 1 1 1 x
0 0 0 0 0 0 0 0 1 1 x
0 0 0 0 0 0 0 1 1 1 x
0 0 0 0 0 0 1 0 1 X x
0 0 0 0 0 0 1 1 1 X 0
0 0 0 0 0 0 0 0 1 0 0
0 0 0 0 0 0 0 1 1 0 0
0 0 0 0 0 0 0 0 1 0 0
0 0 0 0 0 0 0 1 1 0 0
0 0 0 0 0 0 0 0 1 0 0
0 0 0 0 0 0 0 1 1 0 68
0 0 0 0 0 0 0 0 1 0 68
0 0 0 0 0 0 0 1 1 0 0
0 0 0 0 0 0 0 0 1 0 0
0 0 0 0 0 0 0 1 1 0 0
0 0 0 0 0 0 0 0 1 0 0
0 0 0 0 0 0 0 1 1 0 0
0 0 0 0 0 0 0 0 1 0 0
0 0 0 0 0 0 0 1 1 0 0
0 0 0 0 0 0 0 0 1 0 0
0 0 0 0 0 0 0 1 1 0 0
0 0 0 0 0 0 0 0 1 0 0
0 0 0 0 0 0 0 1 1 0 0
0 0 0 0 0 0 0 0 1 0 0
0 0 0 0 0 0 0 1 1 0 0
0 0 0 0 0 0 0 0 1 0 0
0 0 0 0 0 0 0 1 1 0 0
0 0 0 0 0 0 0 0 1 0 0
0 0 0 0 0 0 0 1 1 0 0
0 0 0 0 0 0 0 0 1 0 0
0 0 0 0 0 0 0 1 1 0 0
0 0 0 0 0 0 0 0 1 0 0
0 0 0 0 0 0 0 1 1 0 0
0 0 0 0 0 0 0 0 1 0 0
0 0 0 0 0 0 0 1 1 0 0
0 0 0 0 0 0 0 0 1 0 0
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*/

/* Test case 03_P02T01:
M N progIN reset progLoad start result clk valid done output
0 0 0 0 0 0 0 0 x x x
0 0 0 0 0 0 0 1 x x x
0 0 0 1 0 0 0 0 x x x
0 0 0 1 0 0 0 1 0 0 x
0 0 0 0 0 0 0 0 0 0 x
0 0 0 0 0 0 0 1 0 0 x
0 0 0 0 0 0 0 0 0 0 x
0 0 0 0 0 0 0 1 0 0 x
0 0 0 0 0 0 0 0 0 0 x
0 0 0 0 0 0 0 1 0 0 x
0 0 0 0 0 0 0 0 0 0 x
0 0 0 0 0 0 0 1 0 0 x
0 0 0 0 0 0 0 0 0 0 x
0 0 0 0 0 0 0 1 0 0 x
0 0 0 0 0 0 0 0 0 0 x
0 0 0 0 0 0 0 1 0 0 x
0 0 0 0 0 0 0 0 0 0 x
0 0 0 0 0 0 0 1 0 0 x
0 0 0 0 0 0 0 0 0 0 x
0 0 0 0 0 0 0 1 0 0 x
0 0 0 0 0 0 0 0 0 0 x
0 0 0 0 0 0 0 1 0 0 x
0 0 0 0 0 0 0 0 0 0 x
0 0 0 0 0 0 0 1 0 0 x
0 0 0 0 0 0 0 0 0 0 x
0 0 0 0 0 0 0 1 0 0 x
0 0 0 0 0 0 0 0 0 0 x
0 0 0 0 0 0 0 1 0 0 x
0 0 0 0 0 0 0 0 0 0 x
0 0 0 0 0 0 0 1 0 0 x
0 0 0 0 0 0 0 0 0 0 x
0 0 0 0 0 0 0 1 0 0 x
0 0 0 0 0 0 0 0 0 0 x
0 0 0 0 0 0 0 1 0 0 x
0 0 0 0 0 0 0 0 0 0 x
0 0 0 0 0 0 0 1 0 0 x
0 0 0 0 0 0 0 0 0 0 x
0 0 0 0 0 0 0 1 0 0 x
0 0 0 0 0 0 0 0 0 0 x
0 0 0 0 0 0 0 1 0 0 x
0 0 0 0 0 0 0 0 0 0 x
0 0 0 0 0 0 0 1 0 0 x
0 0 271 0 1 0 0 0 0 0 x
0 0 271 0 1 0 0 1 0 0 x
0 0 566 0 1 0 0 0 0 0 x
0 0 566 0 1 0 0 1 0 0 x
0 0 5888 0 1 0 0 0 0 0 x
0 0 5888 0 1 0 0 1 0 0 x
0 0 3599 0 1 0 0 0 0 0 x
0 0 3599 0 1 0 0 1 0 0 x
0 0 4110 0 1 0 0 0 0 0 x
0 0 4110 0 1 0 0 1 0 0 x
0 0 3856 0 1 0 0 0 0 0 x
0 0 3856 0 1 0 0 1 0 0 x
0 0 7936 0 1 0 0 0 0 0 x
0 0 7936 0 1 0 0 1 0 0 x
0 0 0 0 1 0 0 0 0 0 x
0 0 0 0 1 0 0 1 0 0 x
0 0 0 0 1 0 0 0 0 0 x
0 0 0 0 1 0 0 1 0 0 x
0 0 0 0 1 0 0 0 0 0 x
0 0 0 0 1 0 0 1 0 0 x
0 0 0 0 1 0 0 0 0 0 x
0 0 0 0 1 0 0 1 0 0 x
0 0 0 0 1 0 0 0 0 0 x
0 0 0 0 1 0 0 1 0 0 x
0 0 0 0 1 0 0 0 0 0 x
0 0 0 0 1 0 0 1 0 0 x
0 0 0 0 1 0 0 0 0 0 x
0 0 0 0 1 0 0 1 0 0 x
0 0 0 0 1 0 0 0 0 0 x
0 0 0 0 1 0 0 1 0 0 x
0 0 0 0 1 0 0 0 0 0 x
0 0 0 0 1 0 0 1 0 0 x
0 0 4352 0 1 0 0 0 0 0 x
0 0 4352 0 1 0 0 1 0 0 x
0 0 2819 0 1 0 0 0 0 0 x
0 0 2819 0 1 0 0 1 0 0 x
0 0 7936 0 1 0 0 0 0 0 x
0 0 7936 0 1 0 0 1 0 0 x
0 0 0 0 1 0 0 0 0 0 x
0 0 0 0 1 0 0 1 0 0 x
0 0 0 0 0 0 0 0 0 0 x
0 0 0 0 0 0 0 1 0 0 x
0 0 0 0 0 0 0 0 0 0 x
0 0 0 0 0 0 0 1 0 0 x
0 0 0 0 0 0 0 0 0 0 x
0 0 0 0 0 0 0 1 0 0 x
0 0 0 0 0 1 0 0 0 0 x
0 0 0 0 0 1 0 1 0 0 x
0 0 0 0 0 0 0 0 x 0 x
0 0 0 0 0 0 0 1 x 0 x
0 0 0 0 0 0 0 0 x 0 x
0 0 0 0 0 0 0 1 x 0 x
0 0 0 0 0 0 0 0 x 0 x
0 0 0 0 0 0 0 1 x 0 x
0 0 0 0 0 0 0 0 x 0 x
0 0 0 0 0 0 0 1 x 0 x
0 0 0 0 0 0 0 0 x 0 x
0 0 0 0 0 0 0 1 x 0 x
0 0 0 0 0 0 0 0 x 0 x
0 0 0 0 0 0 0 1 x 0 x
0 0 0 0 0 0 0 0 x 0 x
0 0 0 0 0 0 0 1 x 0 x
0 0 0 0 0 0 0 0 x 0 x
0 0 0 0 0 0 0 1 x 0 x
0 0 0 0 0 0 0 0 x 0 x
0 0 0 0 0 0 0 1 x 0 x
0 0 0 0 0 0 0 0 x 0 x
0 0 0 0 0 0 0 1 x 0 x
0 0 0 0 0 0 0 0 x 0 x
0 0 0 0 0 0 0 1 x 0 x
0 0 0 0 0 0 0 0 x 0 x
0 0 0 0 0 0 0 1 x 0 x
0 0 0 0 0 0 0 0 x 0 x
0 0 0 0 0 0 0 1 x 0 x
0 0 0 0 0 0 0 0 x 0 x
0 0 0 0 0 0 0 1 x 0 x
0 0 0 0 0 0 0 0 x 0 x
0 0 0 0 0 0 0 1 x 0 x
0 0 0 0 0 0 0 0 x 0 x
0 0 0 0 0 0 0 1 x 0 x
0 0 0 0 0 0 0 0 x 0 x
0 0 0 0 0 0 0 1 x 0 x
0 0 0 0 0 0 0 0 x 0 x
0 0 0 0 0 0 0 1 x 0 x
0 0 0 0 0 0 0 0 x 0 x
0 0 0 0 0 0 0 1 x 0 x
0 0 0 0 0 0 0 0 x 0 x
0 0 0 0 0 0 0 1 x 0 x
0 0 0 0 0 0 0 0 x 0 x
0 0 0 0 0 0 0 1 x 0 x
0 0 0 0 0 0 0 0 x 0 x
0 0 0 0 0 0 0 1 x 0 x
0 0 0 0 0 0 0 0 x 0 x
0 0 0 0 0 0 0 1 x 0 x
0 0 0 0 0 0 0 0 x 0 x
0 0 0 0 0 0 0 1 x 0 x
0 0 0 0 0 0 0 0 x 0 x
0 0 0 0 0 0 0 1 x 0 x
0 0 0 0 0 0 0 0 x 0 x
0 0 0 0 0 0 0 1 1 0 x
0 0 0 0 0 0 1 0 1 0 x
0 0 0 0 0 0 1 1 1 0 0
0 0 0 0 0 0 0 0 1 0 0
0 0 0 0 0 0 0 1 1 0 0
0 0 0 0 0 0 0 0 1 0 0
0 0 0 0 0 0 0 1 1 0 0
0 0 0 0 0 0 0 0 1 0 0
0 0 0 0 0 0 0 1 1 0 69
0 0 0 0 0 0 0 0 1 0 69
0 0 0 0 0 0 0 1 1 0 0
0 0 0 0 0 0 0 0 1 0 0
0 0 0 0 0 0 0 1 1 0 0
0 0 0 0 0 0 0 0 1 0 0
0 0 0 0 0 0 0 1 1 0 0
0 0 0 0 0 0 0 0 1 0 0
0 0 0 0 0 0 0 1 1 0 0
0 0 0 0 0 0 0 0 1 0 0
0 0 0 0 0 0 0 1 1 0 0
0 0 0 0 0 0 0 0 1 0 0
0 0 0 0 0 0 0 1 1 0 0
0 0 0 0 0 0 0 0 1 0 0
0 0 0 0 0 0 0 1 1 0 0
0 0 0 0 0 0 0 0 1 0 0
0 0 0 0 0 0 0 1 1 0 0
0 0 0 0 0 0 0 0 1 0 0
0 0 0 0 0 0 0 1 1 0 0
0 0 0 0 0 0 0 0 1 0 0
0 0 0 0 0 0 0 1 1 0 0
0 0 0 0 0 0 0 0 1 0 0
0 0 0 0 0 0 0 1 1 0 0
0 0 0 0 0 0 0 0 1 0 0
0 0 0 0 0 0 0 1 1 0 0
0 0 0 0 0 0 0 0 1 0 0
0 0 0 0 0 0 0 1 1 1 x
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*/

/* Test case 04_P03T01:
M N progIN reset progLoad start result clk valid done output
0 0 0 0 0 0 0 0 x x x
0 0 0 0 0 0 0 1 x x x
0 0 0 1 0 0 0 0 x x x
0 0 0 1 0 0 0 1 0 0 x
0 0 0 0 0 0 0 0 0 0 x
0 0 0 0 0 0 0 1 0 0 x
0 0 0 0 0 0 0 0 0 0 x
0 0 0 0 0 0 0 1 0 0 x
0 0 0 0 0 0 0 0 0 0 x
0 0 0 0 0 0 0 1 0 0 x
0 0 0 0 0 0 0 0 0 0 x
0 0 0 0 0 0 0 1 0 0 x
0 0 0 0 0 0 0 0 0 0 x
0 0 0 0 0 0 0 1 0 0 x
0 0 0 0 0 0 0 0 0 0 x
0 0 0 0 0 0 0 1 0 0 x
0 0 0 0 0 0 0 0 0 0 x
0 0 0 0 0 0 0 1 0 0 x
0 0 0 0 0 0 0 0 0 0 x
0 0 0 0 0 0 0 1 0 0 x
0 0 0 0 0 0 0 0 0 0 x
0 0 0 0 0 0 0 1 0 0 x
0 0 0 0 0 0 0 0 0 0 x
0 0 0 0 0 0 0 1 0 0 x
0 0 0 0 0 0 0 0 0 0 x
0 0 0 0 0 0 0 1 0 0 x
0 0 0 0 0 0 0 0 0 0 x
0 0 0 0 0 0 0 1 0 0 x
0 0 0 0 0 0 0 0 0 0 x
0 0 0 0 0 0 0 1 0 0 x
0 0 0 0 0 0 0 0 0 0 x
0 0 0 0 0 0 0 1 0 0 x
0 0 0 0 0 0 0 0 0 0 x
0 0 0 0 0 0 0 1 0 0 x
0 0 0 0 0 0 0 0 0 0 x
0 0 0 0 0 0 0 1 0 0 x
0 0 0 0 0 0 0 0 0 0 x
0 0 0 0 0 0 0 1 0 0 x
0 0 0 0 0 0 0 0 0 0 x
0 0 0 0 0 0 0 1 0 0 x
0 0 0 0 0 0 0 0 0 0 x
0 0 0 0 0 0 0 1 0 0 x
0 0 0 0 0 0 0 0 0 0 x
0 0 0 0 0 0 0 1 0 0 x
0 0 271 0 1 0 0 0 0 0 x
0 0 271 0 1 0 0 1 0 0 x
0 0 565 0 1 0 0 0 0 0 x
0 0 565 0 1 0 0 1 0 0 x
0 0 2309 0 1 0 0 0 0 0 x
0 0 2309 0 1 0 0 1 0 0 x
0 0 4352 0 1 0 0 0 0 0 x
0 0 4352 0 1 0 0 1 0 0 x
0 0 2818 0 1 0 0 0 0 0 x
0 0 2818 0 1 0 0 1 0 0 x
0 0 2311 0 1 0 0 0 0 0 x
0 0 2311 0 1 0 0 1 0 0 x
0 0 4366 0 1 0 0 0 0 0 x
0 0 4366 0 1 0 0 1 0 0 x
0 0 12 0 1 0 0 0 0 0 x
0 0 12 0 1 0 0 1 0 0 x
0 0 4359 0 1 0 0 0 0 0 x
0 0 4359 0 1 0 0 1 0 0 x
0 0 2819 0 1 0 0 0 0 0 x
0 0 2819 0 1 0 0 1 0 0 x
0 0 7936 0 1 0 0 0 0 0 x
0 0 7936 0 1 0 0 1 0 0 x
0 0 0 0 0 0 0 0 0 0 x
0 0 0 0 0 0 0 1 0 0 x
0 0 0 0 0 0 0 0 0 0 x
0 0 0 0 0 0 0 1 0 0 x
0 0 0 0 0 0 0 0 0 0 x
0 0 0 0 0 0 0 1 0 0 x
0 0 0 0 0 0 0 0 0 0 x
0 0 0 0 0 0 0 1 0 0 x
0 0 0 0 0 0 0 0 0 0 x
0 0 0 0 0 0 0 1 0 0 x
0 0 0 0 0 0 0 0 0 0 x
0 0 0 0 0 0 0 1 0 0 x
0 0 0 0 0 0 0 0 0 0 x
0 0 0 0 0 0 0 1 0 0 x
0 0 0 0 0 0 0 0 0 0 x
0 0 0 0 0 0 0 1 0 0 x
0 0 0 0 0 0 0 0 0 0 x
0 0 0 0 0 0 0 1 0 0 x
0 0 0 0 0 0 0 0 0 0 x
0 0 0 0 0 0 0 1 0 0 x
0 0 0 0 0 0 0 0 0 0 x
0 0 0 0 0 0 0 1 0 0 x
0 0 0 0 0 0 0 0 0 0 x
0 0 0 0 0 0 0 1 0 0 x
0 0 0 0 0 1 0 0 0 0 x
0 0 0 0 0 1 0 1 0 0 x
0 0 0 0 0 0 0 0 x 0 x
0 0 0 0 0 0 0 1 x 0 x
0 0 0 0 0 0 0 0 x 0 x
0 0 0 0 0 0 0 1 x 0 x
0 0 0 0 0 0 0 0 x 0 x
0 0 0 0 0 0 0 1 x 0 x
0 0 0 0 0 0 0 0 x 0 x
0 0 0 0 0 0 0 1 x 0 x
0 0 0 0 0 0 0 0 x 0 x
0 0 0 0 0 0 0 1 x 0 x
0 0 0 0 0 0 0 0 x 0 x
0 0 0 0 0 0 0 1 x 0 x
0 0 0 0 0 0 0 0 x 0 x
0 0 0 0 0 0 0 1 x 0 x
0 0 0 0 0 0 0 0 x 0 x
0 0 0 0 0 0 0 1 x 0 x
0 0 0 0 0 0 0 0 x 0 x
0 0 0 0 0 0 0 1 x 0 x
0 0 0 0 0 0 0 0 x 0 x
0 0 0 0 0 0 0 1 x 0 x
0 0 0 0 0 0 0 0 x 0 x
0 0 0 0 0 0 0 1 x 0 x
0 0 0 0 0 0 0 0 x 0 x
0 0 0 0 0 0 0 1 x 0 x
0 0 0 0 0 0 0 0 x 0 x
0 0 0 0 0 0 0 1 x 0 x
0 0 0 0 0 0 0 0 x 0 x
0 0 0 0 0 0 0 1 x 0 x
0 0 0 0 0 0 0 0 x 0 x
0 0 0 0 0 0 0 1 x 0 x
0 0 0 0 0 0 0 0 x 0 x
0 0 0 0 0 0 0 1 x 0 x
0 0 0 0 0 0 0 0 x 0 x
0 0 0 0 0 0 0 1 x 0 x
0 0 0 0 0 0 0 0 x 0 x
0 0 0 0 0 0 0 1 x 0 x
0 0 0 0 0 0 0 0 x 0 x
0 0 0 0 0 0 0 1 x 0 x
0 0 0 0 0 0 0 0 x 0 x
0 0 0 0 0 0 0 1 x 0 x
0 0 0 0 0 0 0 0 x 0 x
0 0 0 0 0 0 0 1 x 0 x
0 0 0 0 0 0 0 0 x 0 x
0 0 0 0 0 0 0 1 x 0 x
0 0 0 0 0 0 0 0 x 0 x
0 0 0 0 0 0 0 1 x 0 x
0 0 0 0 0 0 0 0 x 0 x
0 0 0 0 0 0 0 1 x 0 x
0 0 0 0 0 0 0 0 x 0 x
0 0 0 0 0 0 0 1 x 0 x
0 0 0 0 0 0 0 0 x 0 x
0 0 0 0 0 0 0 1 1 0 x
0 0 0 0 0 0 1 0 1 0 x
0 0 0 0 0 0 1 1 1 0 0
0 0 0 0 0 0 0 0 1 0 0
0 0 0 0 0 0 0 1 1 0 0
0 0 0 0 0 0 0 0 1 0 0
0 0 0 0 0 0 0 1 1 0 60
0 0 0 0 0 0 0 0 1 0 60
0 0 0 0 0 0 0 1 1 0 118
0 0 0 0 0 0 0 0 1 0 118
0 0 0 0 0 0 0 1 1 0 0
0 0 0 0 0 0 0 0 1 0 0
0 0 0 0 0 0 0 1 1 0 0
0 0 0 0 0 0 0 0 1 0 0
0 0 0 0 0 0 0 1 1 0 0
0 0 0 0 0 0 0 0 1 0 0
0 0 0 0 0 0 0 1 1 0 0
0 0 0 0 0 0 0 0 1 0 0
0 0 0 0 0 0 0 1 1 0 0
0 0 0 0 0 0 0 0 1 0 0
0 0 0 0 0 0 0 1 1 0 0
0 0 0 0 0 0 0 0 1 0 0
0 0 0 0 0 0 0 1 1 0 0
0 0 0 0 0 0 0 0 1 0 0
0 0 0 0 0 0 0 1 1 0 0
0 0 0 0 0 0 0 0 1 0 0
0 0 0 0 0 0 0 1 1 0 0
0 0 0 0 0 0 0 0 1 0 0
0 0 0 0 0 0 0 1 1 0 0
0 0 0 0 0 0 0 0 1 0 0
0 0 0 0 0 0 0 1 1 0 0
0 0 0 0 0 0 0 0 1 0 0
0 0 0 0 0 0 0 1 1 0 0
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*/

/* Test case 05_P04T01:
M N progIN reset progLoad start result clk valid done output
0 0 0 0 0 0 0 0 x x x
0 0 0 0 0 0 0 1 x x x
0 0 0 1 0 0 0 0 x x x
0 0 0 1 0 0 0 1 0 0 x
0 0 0 0 0 0 0 0 0 0 x
0 0 0 0 0 0 0 1 0 0 x
0 0 0 0 0 0 0 0 0 0 x
0 0 0 0 0 0 0 1 0 0 x
0 0 0 0 0 0 0 0 0 0 x
0 0 0 0 0 0 0 1 0 0 x
0 0 0 0 0 0 0 0 0 0 x
0 0 0 0 0 0 0 1 0 0 x
0 0 0 0 0 0 0 0 0 0 x
0 0 0 0 0 0 0 1 0 0 x
0 0 0 0 0 0 0 0 0 0 x
0 0 0 0 0 0 0 1 0 0 x
0 0 0 0 0 0 0 0 0 0 x
0 0 0 0 0 0 0 1 0 0 x
0 0 0 0 0 0 0 0 0 0 x
0 0 0 0 0 0 0 1 0 0 x
0 0 0 0 0 0 0 0 0 0 x
0 0 0 0 0 0 0 1 0 0 x
0 0 0 0 0 0 0 0 0 0 x
0 0 0 0 0 0 0 1 0 0 x
0 0 0 0 0 0 0 0 0 0 x
0 0 0 0 0 0 0 1 0 0 x
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*/

/* Test case 06_P05T01:
M N progIN reset progLoad start result clk valid done output
0 0 0 0 0 0 0 0 x x x
0 0 0 0 0 0 0 1 x x x
0 0 0 1 0 0 0 0 x x x
0 0 0 1 0 0 0 1 0 0 x
0 0 0 0 0 0 0 0 0 0 x
0 0 0 0 0 0 0 1 0 0 x
0 0 0 0 0 0 0 0 0 0 x
0 0 0 0 0 0 0 1 0 0 x
0 0 0 0 0 0 0 0 0 0 x
0 0 0 0 0 0 0 1 0 0 x
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*/

/* Test case 07_P06T01:
M N progIN reset progLoad start result clk valid done output
0 0 0 0 0 0 0 0 x x x
0 0 0 0 0 0 0 1 x x x
0 0 0 1 0 0 0 0 x x x
0 0 0 1 0 0 0 1 0 0 x
0 0 0 0 0 0 0 0 0 0 x
0 0 0 0 0 0 0 1 0 0 x
0 0 0 0 0 0 0 0 0 0 x
0 0 0 0 0 0 0 1 0 0 x
0 0 0 0 0 0 0 0 0 0 x
0 0 0 0 0 0 0 1 0 0 x
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*/

/* Test case 08_P06T02:
M N progIN reset progLoad start result clk valid done output
0 0 0 0 0 0 0 0 x x x
0 0 0 0 0 0 0 1 x x x
0 0 0 1 0 0 0 0 x x x
0 0 0 1 0 0 0 1 0 0 x
0 0 0 0 0 0 0 0 0 0 x
0 0 0 0 0 0 0 1 0 0 x
0 0 0 0 0 0 0 0 0 0 x
0 0 0 0 0 0 0 1 0 0 x
0 0 0 0 0 0 0 0 0 0 x
0 0 0 0 0 0 0 1 0 0 x
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*/

/* Test case 09_P07T01:
M N progIN reset progLoad start result clk valid done output
0 0 0 0 0 0 0 0 x x x
0 0 0 0 0 0 0 1 x x x
0 0 0 1 0 0 0 0 x x x
0 0 0 1 0 0 0 1 0 0 x
0 0 0 0 0 0 0 0 0 0 x
0 0 0 0 0 0 0 1 0 0 x
0 0 0 0 0 0 0 0 0 0 x
0 0 0 0 0 0 0 1 0 0 x
0 0 0 0 0 0 0 0 0 0 x
0 0 0 0 0 0 0 1 0 0 x
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*/

/* Test case 10_P07T02:
M N progIN reset progLoad start result clk valid done output
0 0 0 0 0 0 0 0 x x x
0 0 0 0 0 0 0 1 x x x
0 0 0 1 0 0 0 0 x x x
0 0 0 1 0 0 0 1 0 0 x
0 0 0 0 0 0 0 0 0 0 x
0 0 0 0 0 0 0 1 0 0 x
0 0 0 0 0 0 0 0 0 0 x
0 0 0 0 0 0 0 1 0 0 x
0 0 0 0 0 0 0 0 0 0 x
0 0 0 0 0 0 0 1 0 0 x
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*/

/* Test case 011_P08T01:
M N progIN reset progLoad start result clk valid done output
0 0 0 0 0 0 0 0 x x x
0 0 0 0 0 0 0 1 x x x
0 0 0 1 0 0 0 0 x x x
0 0 0 1 0 0 0 1 0 0 x
0 0 0 0 0 0 0 0 0 0 x
0 0 0 0 0 0 0 1 0 0 x
0 0 0 0 0 0 0 0 0 0 x
0 0 0 0 0 0 0 1 0 0 x
0 0 0 0 0 0 0 0 0 0 x
0 0 0 0 0 0 0 1 0 0 x
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*/

/* Test case 012_P08T02:
M N progIN reset progLoad start result clk valid done output
0 0 0 0 0 0 0 0 x x x
0 0 0 0 0 0 0 1 x x x
0 0 0 1 0 0 0 0 x x x
0 0 0 1 0 0 0 1 0 0 x
0 0 0 0 0 0 0 0 0 0 x
0 0 0 0 0 0 0 1 0 0 x
0 0 0 0 0 0 0 0 0 0 x
0 0 0 0 0 0 0 1 0 0 x
0 0 0 0 0 0 0 0 0 0 x
0 0 0 0 0 0 0 1 0 0 x
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*/

/* Test case 013_P09T01:
M N progIN reset progLoad start result clk valid done output
0 0 0 0 0 0 0 0 x x x
0 0 0 0 0 0 0 1 x x x
0 0 0 1 0 0 0 0 x x x
0 0 0 1 0 0 0 1 0 0 x
0 0 0 0 0 0 0 0 0 0 x
0 0 0 0 0 0 0 1 0 0 x
0 0 0 0 0 0 0 0 0 0 x
0 0 0 0 0 0 0 1 0 0 x
0 0 0 0 0 0 0 0 0 0 x
0 0 0 0 0 0 0 1 0 0 x
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*/

/* Test case 014_P09T02:
M N progIN reset progLoad start result clk valid done output
0 0 0 0 0 0 0 0 x x x
0 0 0 0 0 0 0 1 x x x
0 0 0 1 0 0 0 0 x x x
0 0 0 1 0 0 0 1 0 0 x
0 0 0 0 0 0 0 0 0 0 x
0 0 0 0 0 0 0 1 0 0 x
0 0 0 0 0 0 0 0 0 0 x
0 0 0 0 0 0 0 1 0 0 x
0 0 0 0 0 0 0 0 0 0 x
0 0 0 0 0 0 0 1 0 0 x
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*/
